// Logisim project MACROSOFT_KHIRKI_9.circ as structural Verilog: 36 circuits, main circuit main
module main (
  input  [7:0] in_1,
  input  in_2,
  input  [7:0] in_3,
  input  [7:0] in_4,
  input  in_5,
  input  in_6,
  input  [7:0] in_7,
  input  in_8,
  input  R0s,
  input  R0e,
  input  R1s,
  input  R1e,
  input  R2s,
  input  R2e,
  input  R3s,
  input  R3e,
  input  PCoe,
  input  MARbs,
  input  PCena,
  input  MARs,
  input  ALUos,
  input  ALUoe,
  input  As,
  input  RAMs,
  input  RAMe,
  input  IARs,
  input  IARe,
  input  IRs,
  input  IRe,
  input  IRRs,
  input  in_31,
  input  in_32
);

  wire alu_8_1_c_out, alu_8_1_neg, alu_8_1_zero, alu_8_2_p5, alu_8_2_p7, alu_8_2_p11, alu_8_2_p12,
       alu_8_2_p13, clock_1_out, clock_2_out, cu_finale_1_p1, cu_finale_1_p2, cu_finale_1_p3, cu_finale_1_p4,
       cu_finale_1_p5, cu_finale_1_p10, cu_finale_1_p11, cu_finale_1_p12, cu_finale_1_p13, cu_finale_1_p14,
       cu_finale_1_p16, cu_finale_1_p18, cu_finale_1_p19, cu_finale_1_p20, cu_finale_1_p21, cu_finale_1_p23,
       cu_finale_1_p25, cu_finale_1_p27, cu_finale_1_p28, cu_finale_1_p29, cu_finale_1_p30;
  wire [3:0] alu_8_2_p6, controlled_buffer_6_out, controlled_buffer_6_out_2, cu_finale_1_p9, mar_1_ireg,
       mar_1_o, mar_2_ireg, mar_2_o;
  wire [7:0] alu_8_1_ra, alu_8_1_ro, controlled_buffer_1_out, controlled_buffer_5_out, counter_1_q,
       cu_finale_1_p22, cu_finale_1_p26, IAR_ireg, IAR_o, IR_ireg, mux_2x1_8bit_1_o, mux_2x1_8bit_2_o, PC_q,
       R0_ireg, R1_ireg, R2_ireg, R3_ireg, ram_1_dout, ram_2_dout, reg_8_1_ireg, reg_8_2_ireg, reg_8_2_o,
       reg_8_3_ireg, reg_8_4_ireg, reg_8_5_ireg, reg_8_5_o, reg_8_6_ireg;

  Counter PC (.D(PC_q), .count(cu_finale_1_p2), .Q(PC_q), .clk(clock_1_out), .clr(in_32));  // open: load, carry, up
  // Probe on alu_8_1_ra
  assign controlled_buffer_1_out = cu_finale_1_p1 ? PC_q : 8'bz;  // Controlled_Buffer controlled_buffer_1
  // Probe on PC_q
  // Probe on alu_8_1_ro
  ALU_8 alu_8_1 (
    .Os(cu_finale_1_p3), .Oe(cu_finale_1_p4), .A(controlled_buffer_1_out), .As(cu_finale_1_p5),
    .B(controlled_buffer_1_out), .sel(cu_finale_1_p9), .clr(in_32), .ro(alu_8_1_ro), .C_out(alu_8_1_c_out),
    .zero(alu_8_1_zero), .NEG(alu_8_1_neg), .O(controlled_buffer_1_out), .ra(alu_8_1_ra));
  Clock clock_1 (.out(clock_1_out));
  // Probe on R0_ireg
  reg_8 R0 (
    .i(controlled_buffer_1_out), .s(cu_finale_1_p10), .e(cu_finale_1_p11), .clr(in_32), .ireg(R0_ireg),
    .o(controlled_buffer_1_out));
  // Probe on IAR_ireg
  // Probe on R1_ireg
  reg_8 R1 (
    .i(controlled_buffer_1_out), .s(cu_finale_1_p14), .e(cu_finale_1_p16), .clr(in_32), .ireg(R1_ireg),
    .o(controlled_buffer_1_out));
  reg_8 IAR (
    .i(controlled_buffer_1_out), .s(cu_finale_1_p12), .e(cu_finale_1_p13), .clr(in_32), .ireg(IAR_ireg),
    .o(IAR_o));
  // CU_finale cu_finale_1: pin names not known; wires that end beside it: cu_finale_1_p1, cu_finale_1_p2, cu_finale_1_p3, cu_finale_1_p4, cu_finale_1_p5, alu_8_1_c_out, alu_8_1_zero, alu_8_1_neg, cu_finale_1_p9, cu_finale_1_p10, cu_finale_1_p11, cu_finale_1_p12, cu_finale_1_p13, cu_finale_1_p14, IAR_o, cu_finale_1_p16, clock_1_out, cu_finale_1_p18, cu_finale_1_p19, cu_finale_1_p20, cu_finale_1_p21, cu_finale_1_p22, cu_finale_1_p23, in_32, cu_finale_1_p25, cu_finale_1_p26, cu_finale_1_p27, cu_finale_1_p28, cu_finale_1_p29, cu_finale_1_p30
  // Probe on R2_ireg
  reg_8 R2 (
    .i(controlled_buffer_1_out), .s(cu_finale_1_p20), .e(cu_finale_1_p21), .clr(in_32), .ireg(R2_ireg),
    .o(controlled_buffer_1_out));
  // Probe on IR_ireg
  reg_8 IR (
    .i(controlled_buffer_1_out), .s(cu_finale_1_p18), .e(cu_finale_1_p19), .clr(in_32), .ireg(IR_ireg),
    .o(cu_finale_1_p22));
  // Probe on controlled_buffer_1_out
  // Probe on R3_ireg
  reg_8 R3 (
    .i(controlled_buffer_1_out), .s(cu_finale_1_p23), .e(cu_finale_1_p25), .clr(in_32), .ireg(R3_ireg),
    .o(controlled_buffer_1_out));
  // Probe on controlled_buffer_1_out
  assign controlled_buffer_1_out = in_2 ? in_1 : 8'bz;  // Controlled_Buffer controlled_buffer_2
  assign controlled_buffer_1_out = in_6 ? in_4 : 8'bz;  // Controlled_Buffer controlled_buffer_3
  MUX_2x1_8bit mux_2x1_8bit_1 (
    .sel(cu_finale_1_p27), .A(controlled_buffer_1_out), .B(cu_finale_1_p26), .O(mux_2x1_8bit_1_o));
  RAM #(.addrWidth(4), .asyncread("true"), .clearpin("true")) ram_1 (
    .addr(mar_1_o), .we(cu_finale_1_p29), .oe(cu_finale_1_p30), .clk(clock_1_out),
    .din(controlled_buffer_1_out), .dout(ram_1_dout));  // open: clr
  // Probe on mar_1_ireg
  MAR mar_1 (.s(cu_finale_1_p28), .clr(in_32), .i(mux_2x1_8bit_1_o), .ireg(mar_1_ireg), .o(mar_1_o));
  assign controlled_buffer_1_out = cu_finale_1_p30 ? ram_1_dout : 8'bz;  // Controlled_Buffer controlled_buffer_4
  // Probe on counter_1_q
  Counter counter_1 (
    .D(counter_1_q), .count(PCena), .Q(counter_1_q), .clk(clock_2_out), .clr(in_31));  // open: load, carry, up
  // Probe on alu_8_2_p5
  assign controlled_buffer_5_out = PCoe ? counter_1_q : 8'bz;  // Controlled_Buffer controlled_buffer_5
  // Probe on alu_8_2_p7
  // ALU_8 alu_8_2: pin names not known; wires that end beside it: controlled_buffer_5_out, As, controlled_buffer_5_out, in_31, alu_8_2_p5, alu_8_2_p6, alu_8_2_p7, controlled_buffer_5_out, ALUos, ALUoe, alu_8_2_p11, alu_8_2_p12, alu_8_2_p13
  Clock clock_2 (.out(clock_2_out));
  // Probe on reg_8_1_ireg
  reg_8 reg_8_1 (
    .i(controlled_buffer_5_out), .s(R0s), .e(R0e), .clr(in_31), .ireg(reg_8_1_ireg),
    .o(controlled_buffer_5_out));
  // Probe on reg_8_2_ireg
  reg_8 reg_8_2 (.i(controlled_buffer_5_out), .s(IARs), .e(IARe), .clr(in_31), .ireg(reg_8_2_ireg), .o(reg_8_2_o));
  // Probe on reg_8_3_ireg
  reg_8 reg_8_3 (
    .i(controlled_buffer_5_out), .s(R1s), .e(R1e), .clr(in_31), .ireg(reg_8_3_ireg),
    .o(controlled_buffer_5_out));
  // Probe on alu_8_2_p6
  assign {controlled_buffer_6_out_2, controlled_buffer_6_out} = IARe ? reg_8_2_o : 8'bz;  // Controlled_Buffer controlled_buffer_6
  // Probe on reg_8_4_ireg
  // Probe on {controlled_buffer_6_out_2, controlled_buffer_6_out}
  // Probe on reg_8_5_ireg
  reg_8 reg_8_4 (
    .i(controlled_buffer_5_out), .s(R2s), .e(R2e), .clr(in_31), .ireg(reg_8_4_ireg),
    .o(controlled_buffer_5_out));
  // Probe on controlled_buffer_6_out
  assign {alu_8_2_p6, controlled_buffer_6_out} = IRe ? reg_8_5_o : 8'bz;  // Controlled_Buffer controlled_buffer_7
  reg_8 reg_8_5 (.i(controlled_buffer_5_out), .s(IRs), .e(IRe), .clr(in_31), .ireg(reg_8_5_ireg), .o(reg_8_5_o));
  // Probe on controlled_buffer_5_out
  // Probe on reg_8_6_ireg
  // Probe on controlled_buffer_5_out
  reg_8 reg_8_6 (
    .i(controlled_buffer_5_out), .s(R3s), .e(R3e), .clr(in_31), .ireg(reg_8_6_ireg),
    .o(controlled_buffer_5_out));
  assign controlled_buffer_5_out = in_5 ? in_3 : 8'bz;  // Controlled_Buffer controlled_buffer_8
  assign controlled_buffer_5_out = in_8 ? in_7 : 8'bz;  // Controlled_Buffer controlled_buffer_9
  // Probe on controlled_buffer_5_out
  MUX_2x1_8bit mux_2x1_8bit_2 (
    .sel(MARbs), .A(controlled_buffer_5_out), .B({controlled_buffer_6_out_2, controlled_buffer_6_out}),
    .O(mux_2x1_8bit_2_o));
  RAM #(.addrWidth(4), .asyncread("true"), .clearpin("true")) ram_2 (
    .addr(mar_2_o), .we(RAMs), .oe(RAMe), .clk(clock_2_out), .din(controlled_buffer_5_out), .dout(ram_2_dout));  // open: clr
  // Probe on mar_2_ireg
  MAR mar_2 (.s(MARs), .clr(in_31), .i(mux_2x1_8bit_2_o), .ireg(mar_2_ireg), .o(mar_2_o));
  assign controlled_buffer_5_out = RAMe ? ram_2_dout : 8'bz;  // Controlled_Buffer controlled_buffer_10
endmodule

module loadim_wo_IAR_MBRs (
  input  [2:0] counter,
  input  [3:0] reg_sel,
  output As,
  output ALUos,
  output ALUoe,
  output R0s,
  output R0e,
  output R1s,
  output R1e,
  output R2s,
  output R2e,
  output R3s,
  output R3e,
  output IRs,
  output IARs,
  output IARe,
  output MARs,
  output RAMs,
  output RAMe,
  output PCena,
  output PCoe,
  output MARbs,
  output IRe,
  output IRRs
);

  wire and_10_out, and_11_out, not_1_out, not_2_out, not_3_out, not_4_out, not_5_out;
  wire [1:0] and_1_out;

  and and_1 (and_1_out[0], reg_sel[0], reg_sel[2]);
  and and_2 (and_1_out[1], reg_sel[1], reg_sel[3]);
  not not_1 (not_1_out, and_1_out[1]);
  not not_2 (not_2_out, and_1_out[0]);
  not not_3 (not_3_out, counter[2]);
  not not_4 (not_4_out, counter[1]);
  not not_5 (not_5_out, counter[0]);
  and and_3 (R0e, not_1_out, not_2_out, not_3_out, counter[1], counter[0]);
  and and_4 (R1e, not_1_out, and_1_out[0], not_3_out, counter[1], counter[0]);
  and and_5 (R2e, and_1_out[1], not_2_out, not_3_out, counter[1], counter[0]);
  and and_6 (R3e, and_1_out[1], and_1_out[0], not_3_out, counter[1], counter[0]);
  and and_7 (IRs, not_3_out, not_4_out, counter[0]);
  and and_8 (MARs, not_3_out, not_5_out);
  and and_9 (RAMe, not_3_out, counter[0]);
  and and_10 (and_10_out, not_3_out, counter[1], not_5_out);
  and and_11 (and_11_out, counter[2], not_4_out, not_5_out);
  and and_12 (PCoe, not_3_out, not_5_out);
  or or_1 (PCena, and_10_out, and_11_out);

  assign ALUoe = 1'b0;
  assign ALUos = 1'b0;
  assign As = 1'b0;
  assign IARe = 1'b0;
  assign IARs = 1'b0;
  assign IRe = 1'b1;
  assign IRRs = 1'b0;
  assign MARbs = 1'b0;
  assign R0s = 1'b0;
  assign R1s = 1'b0;
  assign R2s = 1'b0;
  assign R3s = 1'b0;
  assign RAMs = 1'b0;
endmodule

module CU_finale (
  input  clr,
  input  [7:0] IARin,
  input  cin,
  input  zero,
  input  [7:0] IRin,
  input  neg,
  output As,
  output ALUos,
  output ALUoe,
  output R0s,
  output R0e,
  output R1s,
  output R1e,
  output R2s,
  output R2e,
  output R3s,
  output R3e,
  output IRs,
  output IARs,
  output IARe,
  output MARs,
  output RAMs,
  output RAMe,
  output PCena,
  output PCoe,
  output MARbs,
  output IRe,
  output [7:0] MBRd,
  output [3:0] sel
);

  wire alu_8_1_c_out, alu_8_1_neg, alu_8_1_zero, and_1_out, and_2_out, and_3_out, and_4_out, and_5_out,
       and_6_out, and_7_out, and_8_out, and_9_out, and_10_out, and_11_out, clock_1_out, counter_1_carry,
       cpu_dcode_3x8_w_ena_1_o0, cpu_dcode_3x8_w_ena_1_o1, cpu_dcode_3x8_w_ena_1_o2,
       cpu_dcode_3x8_w_ena_1_o3, cpu_dcode_3x8_w_ena_1_o4, cpu_dcode_3x8_w_ena_1_o5,
       cpu_dcode_3x8_w_ena_2_o0, cpu_dcode_3x8_w_ena_2_o1, cpu_dcode_3x8_w_ena_2_o2,
       cpu_dcode_3x8_w_ena_2_o3, cpu_dcode_3x8_w_ena_2_o4, cpu_dcode_3x8_w_ena_2_o5,
       cpu_dcode_3x8_w_ena_2_o6, cpu_dcode_3x8_w_ena_2_o7, not_1_out, not_2_out, not_3_out, not_4_out,
       not_5_out, not_6_out, not_7_out, not_8_out, not_9_out, not_10_out, not_11_out, not_12_out, not_13_out,
       not_14_out, not_15_out, not_16_out, or_1_out, or_2_out, or_3_out, pull_resistor_1_node, undriven,
       undriven_2;
  wire [1:0] and_27_out, and_31_out, and_32_out;
  wire [3:0] mar_1_ireg, mar_1_o, register_1_q;
  wire [4:0] and_30_out;
  wire [5:4] and_25_out;
  wire [7:0] alu_8_1_ra, alu_8_1_ro, and_15_out, controlled_buffer_1_out, controlled_buffer_2_out,
       counter_1_q, counter_2_q, mux_2x1_8bit_1_o, ram_1_dout, reg_8_1_ireg, reg_8_2_ireg, reg_8_2_o,
       reg_8_3_ireg, reg_8_4_ireg, reg_8_5_ireg, reg_8_5_o, reg_8_6_ireg;
  wire [21:0] andoraddsub_w_propogation_1_as, loadim_final_working_1_as, lw_satrt_at1_finale_1_as,
       mov_starts_at_1_finale_1_as, saveim_final_working_1_as, sw_starts_at_1_finale_1_as;
  wire [21:21] controlled_buffer_3_out;

  Counter #(.max('h5)) counter_1 (
    .load(undriven), .D(counter_1_q), .count(pull_resistor_1_node), .Q(counter_1_q), .carry(counter_1_carry),
    .up(undriven_2), .clk(clock_1_out), .clr(clr));
  Pull_Resistor #(.pull(1)) pull_resistor_1 (.node(pull_resistor_1_node));
  not not_1 (not_1_out, sel[3]);
  Counter counter_2 (
    .D(counter_2_q), .count(and_30_out[1]), .Q(counter_2_q), .clk(clock_1_out), .clr(clr));  // open: load, carry, up
  // Probe on counter_1_q
  not not_2 (not_2_out, sel[1]);
  not not_3 (not_3_out, sel[0]);
  not not_4 (not_4_out, sel[3]);
  not not_5 (not_5_out, sel[1]);
  and and_1 (and_1_out, not_1_out, sel[2], not_2_out, not_3_out);
  and and_2 (and_2_out, not_4_out, sel[2], not_5_out, sel[0]);
  or or_1 (or_1_out, and_1_out, and_2_out);
  // Probe on counter_2_q
  // Probe on alu_8_1_ra
  not not_6 (not_6_out, register_1_q[2]);
  and and_3 (and_3_out, register_1_q[3], register_1_q[2], register_1_q[1], register_1_q[0]);
  and and_4 (and_4_out, or_1_out, or_2_out);
  assign controlled_buffer_1_out = and_30_out[0] ? counter_2_q : 8'bz;  // Controlled_Buffer controlled_buffer_1
  not not_7 (not_7_out, register_1_q[0]);
  not not_8 (not_8_out, register_1_q[3]);
  not not_9 (not_9_out, register_1_q[1]);
  and and_5 (and_5_out, register_1_q[3], not_6_out, register_1_q[1], not_7_out);
  and and_6 (and_6_out, not_8_out, register_1_q[2], not_9_out, register_1_q[0]);
  or or_2 (or_2_out, and_3_out, and_5_out, and_6_out, and_7_out);
  // Probe on alu_8_1_ro
  ALU_8 alu_8_1 (
    .Os(and_30_out[2]), .Oe(and_30_out[3]), .A(controlled_buffer_1_out), .As(and_30_out[4]),
    .B(controlled_buffer_1_out), .sel(sel), .clr(clr), .ro(alu_8_1_ro), .C_out(alu_8_1_c_out),
    .zero(alu_8_1_zero), .NEG(alu_8_1_neg), .O(controlled_buffer_1_out), .ra(alu_8_1_ra));
  not not_10 (not_10_out, register_1_q[3]);
  not not_11 (not_11_out, register_1_q[2]);
  not not_12 (not_12_out, register_1_q[1]);
  not not_13 (not_13_out, register_1_q[0]);
  and and_7 (and_7_out, not_10_out, not_11_out, not_12_out, not_13_out);
  Clock clock_1 (.out(clock_1_out));
  LED led_1 (.in(cin));
  LED led_2 (.in(zero));
  LED led_3 (.in(neg));
  Pull_Resistor pull_resistor_2 (.node(controlled_buffer_1_out));
  // Probe on reg_8_1_ireg
  reg_8 reg_8_1 (
    .i(controlled_buffer_1_out), .s(and_15_out[0]), .e(and_15_out[1]), .clr(clr), .ireg(reg_8_1_ireg),
    .o(controlled_buffer_1_out));
  Register #(.trigger("falling")) register_1 (
    .D(IRin), .en(IRe), .clk(clock_1_out), .Q({sel, register_1_q}), .clr(clr));
  // Probe on reg_8_3_ireg
  // Probe on reg_8_2_ireg
  assign controlled_buffer_2_out = and_25_out[4] ? reg_8_2_o : 8'bz;  // Controlled_Buffer controlled_buffer_2
  reg_8 reg_8_2 (
    .i(controlled_buffer_1_out), .s(and_25_out[5]), .e(and_25_out[4]), .clr(clr), .ireg(reg_8_2_ireg),
    .o(reg_8_2_o));
  // Probe on controlled_buffer_1_out
  reg_8 reg_8_3 (
    .i(controlled_buffer_1_out), .s(and_15_out[2]), .e(and_15_out[3]), .clr(clr), .ireg(reg_8_3_ireg),
    .o(controlled_buffer_1_out));
  // Probe on {sel, register_1_q}
  // Probe on reg_8_4_ireg
  // Probe on reg_8_5_ireg
  // Probe on IARin
  // Probe on IRin
  reg_8 reg_8_4 (
    .i(controlled_buffer_1_out), .s(and_15_out[4]), .e(and_15_out[5]), .clr(clr), .ireg(reg_8_4_ireg),
    .o(controlled_buffer_1_out));
  reg_8 reg_8_5 (
    .i(controlled_buffer_1_out), .s(and_32_out[1]), .e(and_32_out[0]), .clr(clr), .ireg(reg_8_5_ireg),
    .o(reg_8_5_o));
  Pull_Resistor pull_resistor_3 (.node(IRin));
  andoraddsub_w_propogation andoraddsub_w_propogation_1 (
    .count(counter_1_q[2:0]), .reg_sel(register_1_q), .As(andoraddsub_w_propogation_1_as[0]),
    .ALUos(andoraddsub_w_propogation_1_as[1]), .ALUoe(andoraddsub_w_propogation_1_as[2]),
    .R0s(andoraddsub_w_propogation_1_as[3]), .R0e(andoraddsub_w_propogation_1_as[4]),
    .R1s(andoraddsub_w_propogation_1_as[5]), .R1e(andoraddsub_w_propogation_1_as[6]),
    .R2s(andoraddsub_w_propogation_1_as[7]), .R2e(andoraddsub_w_propogation_1_as[8]),
    .R3s(andoraddsub_w_propogation_1_as[9]), .R3e(andoraddsub_w_propogation_1_as[10]),
    .IRs(andoraddsub_w_propogation_1_as[11]), .IARs(andoraddsub_w_propogation_1_as[12]),
    .IARe(andoraddsub_w_propogation_1_as[13]), .MARs(andoraddsub_w_propogation_1_as[14]),
    .RAMs(andoraddsub_w_propogation_1_as[15]), .RAMe(andoraddsub_w_propogation_1_as[16]),
    .PCena(andoraddsub_w_propogation_1_as[17]), .PCoe(andoraddsub_w_propogation_1_as[18]),
    .MARbs(andoraddsub_w_propogation_1_as[19]), .IRe(andoraddsub_w_propogation_1_as[20]));
  Pull_Resistor pull_resistor_4 (.node(andoraddsub_w_propogation_1_as[21]));
  LW_satrt_at1_finale lw_satrt_at1_finale_1 (
    .count(counter_1_q[2:0]), .op_code(register_1_q), .As(lw_satrt_at1_finale_1_as[0]),
    .ALUos(lw_satrt_at1_finale_1_as[1]), .ALUoe(lw_satrt_at1_finale_1_as[2]),
    .R0s(lw_satrt_at1_finale_1_as[3]), .R0e(lw_satrt_at1_finale_1_as[4]), .R1s(lw_satrt_at1_finale_1_as[5]),
    .R1e(lw_satrt_at1_finale_1_as[6]), .R2s(lw_satrt_at1_finale_1_as[7]), .R2e(lw_satrt_at1_finale_1_as[8]),
    .R3s(lw_satrt_at1_finale_1_as[9]), .R3e(lw_satrt_at1_finale_1_as[10]),
    .IRs(lw_satrt_at1_finale_1_as[11]), .IARs(lw_satrt_at1_finale_1_as[12]),
    .IARe(lw_satrt_at1_finale_1_as[13]), .MARs(lw_satrt_at1_finale_1_as[14]),
    .RAMs(lw_satrt_at1_finale_1_as[15]), .RAMe(lw_satrt_at1_finale_1_as[16]),
    .PCena(lw_satrt_at1_finale_1_as[17]));
  Pull_Resistor pull_resistor_5 (.node(lw_satrt_at1_finale_1_as[21]));
  LOADim_FINAL_WORKING loadim_final_working_1 (
    .counter(counter_1_q[2:0]), .reg_sel(register_1_q), .As(loadim_final_working_1_as[0]),
    .ALUos(loadim_final_working_1_as[1]), .ALUoe(loadim_final_working_1_as[2]),
    .R0s(loadim_final_working_1_as[3]), .R0e(loadim_final_working_1_as[4]),
    .R1s(loadim_final_working_1_as[5]), .R1e(loadim_final_working_1_as[6]),
    .R2s(loadim_final_working_1_as[7]), .R2e(loadim_final_working_1_as[8]),
    .R3s(loadim_final_working_1_as[9]), .R3e(loadim_final_working_1_as[10]),
    .IRs(loadim_final_working_1_as[11]), .IARs(loadim_final_working_1_as[12]),
    .IARe(loadim_final_working_1_as[13]), .MARs(loadim_final_working_1_as[14]),
    .RAMs(loadim_final_working_1_as[15]), .RAMe(loadim_final_working_1_as[16]),
    .PCena(loadim_final_working_1_as[17]), .PCoe(loadim_final_working_1_as[18]),
    .MARbs(loadim_final_working_1_as[19]), .IRe(loadim_final_working_1_as[20]),
    .IRRs(loadim_final_working_1_as[21]));
  SW_starts_at_1_finale sw_starts_at_1_finale_1 (
    .count(counter_1_q[2:0]), .op_code(register_1_q), .As(sw_starts_at_1_finale_1_as[0]),
    .ALUos(sw_starts_at_1_finale_1_as[1]), .ALUoe(sw_starts_at_1_finale_1_as[2]),
    .R0s(sw_starts_at_1_finale_1_as[3]), .R0e(sw_starts_at_1_finale_1_as[4]),
    .R1s(sw_starts_at_1_finale_1_as[5]), .R1e(sw_starts_at_1_finale_1_as[6]),
    .R2s(sw_starts_at_1_finale_1_as[7]), .R2e(sw_starts_at_1_finale_1_as[8]),
    .R3s(sw_starts_at_1_finale_1_as[9]), .R3e(sw_starts_at_1_finale_1_as[10]),
    .IRs(sw_starts_at_1_finale_1_as[11]), .IARs(sw_starts_at_1_finale_1_as[12]),
    .IARe(sw_starts_at_1_finale_1_as[13]), .MARs(sw_starts_at_1_finale_1_as[14]),
    .RAMs(sw_starts_at_1_finale_1_as[15]), .RAMe(sw_starts_at_1_finale_1_as[16]),
    .PCena(sw_starts_at_1_finale_1_as[17]));
  Pull_Resistor pull_resistor_6 (.node(sw_starts_at_1_finale_1_as[21]));
  SAVEim_FINAL_WORKING saveim_final_working_1 (
    .counter(counter_1_q[2:0]), .reg_sel(register_1_q), .As(saveim_final_working_1_as[0]),
    .ALUos(saveim_final_working_1_as[1]), .ALUoe(saveim_final_working_1_as[2]),
    .R0s(saveim_final_working_1_as[3]), .R0e(saveim_final_working_1_as[4]),
    .R1s(saveim_final_working_1_as[5]), .R1e(saveim_final_working_1_as[6]),
    .R2s(saveim_final_working_1_as[7]), .R2e(saveim_final_working_1_as[8]),
    .R3s(saveim_final_working_1_as[9]), .R3e(saveim_final_working_1_as[10]),
    .IRs(saveim_final_working_1_as[11]), .IARs(saveim_final_working_1_as[12]),
    .IARe(saveim_final_working_1_as[13]), .MARs(saveim_final_working_1_as[14]),
    .RAMs(saveim_final_working_1_as[15]), .RAMe(saveim_final_working_1_as[16]),
    .PCena(saveim_final_working_1_as[17]), .PCoe(saveim_final_working_1_as[18]),
    .MARbs(saveim_final_working_1_as[19]), .IRe(saveim_final_working_1_as[20]),
    .IRRs(saveim_final_working_1_as[21]));
  MOV_starts_at_1_finale mov_starts_at_1_finale_1 (
    .count(counter_1_q[2:0]), .op_code(register_1_q), .As(mov_starts_at_1_finale_1_as[0]),
    .ALUos(mov_starts_at_1_finale_1_as[1]), .ALUoe(mov_starts_at_1_finale_1_as[2]),
    .R0s(mov_starts_at_1_finale_1_as[3]), .R0e(mov_starts_at_1_finale_1_as[4]),
    .R1s(mov_starts_at_1_finale_1_as[5]), .R1e(mov_starts_at_1_finale_1_as[6]),
    .R2s(mov_starts_at_1_finale_1_as[7]), .R2e(mov_starts_at_1_finale_1_as[8]),
    .R3s(mov_starts_at_1_finale_1_as[9]), .R3e(mov_starts_at_1_finale_1_as[10]),
    .IRs(mov_starts_at_1_finale_1_as[11]), .IARs(mov_starts_at_1_finale_1_as[12]),
    .IARe(mov_starts_at_1_finale_1_as[13]), .MARs(mov_starts_at_1_finale_1_as[14]),
    .RAMs(mov_starts_at_1_finale_1_as[15]), .RAMe(mov_starts_at_1_finale_1_as[16]),
    .PCena(mov_starts_at_1_finale_1_as[17]));
  Pull_Resistor pull_resistor_7 (.node(mov_starts_at_1_finale_1_as[21]));
  // Probe on reg_8_6_ireg
  // Probe on controlled_buffer_1_out
  reg_8 reg_8_6 (
    .i(controlled_buffer_1_out), .s(and_15_out[6]), .e(and_15_out[7]), .clr(clr), .ireg(reg_8_6_ireg),
    .o(controlled_buffer_1_out));
  Pull_Resistor pull_resistor_8 (.node(andoraddsub_w_propogation_1_as));
  RAM #(.addrWidth(4), .asyncread("true"), .clearpin("true")) ram_1 (
    .addr(mar_1_o), .we(and_27_out[0]), .oe(and_27_out[1]), .clk(clock_1_out), .din(controlled_buffer_1_out),
    .dout(ram_1_dout));  // open: clr
  not not_14 (not_14_out, sel[3]);
  and and_8 (and_8_out, and_4_out, cpu_dcode_3x8_w_ena_2_o4);
  assign {controlled_buffer_3_out[21], IRe, MARbs, PCoe, PCena, RAMe, RAMs, MARs, IARe, IARs, IRs, R3e, R3s, R2e, R2s, R1e, R1s, R0e, R0s, ALUoe, ALUos, As} = and_8_out ? loadim_final_working_1_as : 22'bz;  // Controlled_Buffer controlled_buffer_3
  and and_9 (and_9_out, and_4_out, cpu_dcode_3x8_w_ena_2_o5);
  assign {controlled_buffer_3_out[21], IRe, MARbs, PCoe, PCena, RAMe, RAMs, MARs, IARe, IARs, IRs, R3e, R3s, R2e, R2s, R1e, R1s, R0e, R0s, ALUoe, ALUos, As} = and_9_out ? saveim_final_working_1_as : 22'bz;  // Controlled_Buffer controlled_buffer_4
  MUX_2x1_8bit mux_2x1_8bit_1 (.sel(and_31_out[0]), .A(controlled_buffer_1_out), .B(IARin), .O(mux_2x1_8bit_1_o));
  CPU_DCODE_3x8_w_ena cpu_dcode_3x8_w_ena_1 (
    .Sel(sel[2:0]), .enable(sel[3]), .O0(cpu_dcode_3x8_w_ena_1_o0), .O1(cpu_dcode_3x8_w_ena_1_o1),
    .O2(cpu_dcode_3x8_w_ena_1_o2), .O3(cpu_dcode_3x8_w_ena_1_o3), .O4(cpu_dcode_3x8_w_ena_1_o4),
    .O5(cpu_dcode_3x8_w_ena_1_o5));  // open: O6, O7
  // Probe on mar_1_ireg
  MAR mar_1 (.s(and_31_out[1]), .clr(clr), .i(mux_2x1_8bit_1_o), .ireg(mar_1_ireg), .o(mar_1_o));
  CPU_DCODE_3x8_w_ena cpu_dcode_3x8_w_ena_2 (
    .Sel(sel[2:0]), .enable(not_14_out), .O0(cpu_dcode_3x8_w_ena_2_o0), .O1(cpu_dcode_3x8_w_ena_2_o1),
    .O2(cpu_dcode_3x8_w_ena_2_o2), .O3(cpu_dcode_3x8_w_ena_2_o3), .O4(cpu_dcode_3x8_w_ena_2_o4),
    .O5(cpu_dcode_3x8_w_ena_2_o5), .O6(cpu_dcode_3x8_w_ena_2_o6), .O7(cpu_dcode_3x8_w_ena_2_o7));
  or or_3 (or_3_out, cpu_dcode_3x8_w_ena_2_o3, cpu_dcode_3x8_w_ena_2_o2, cpu_dcode_3x8_w_ena_2_o1, cpu_dcode_3x8_w_ena_2_o0);
  assign {controlled_buffer_3_out[21], IRe, MARbs, PCoe, PCena, RAMe, RAMs, MARs, IARe, IARs, IRs, R3e, R3s, R2e, R2s, R1e, R1s, R0e, R0s, ALUoe, ALUos, As} = or_3_out ? andoraddsub_w_propogation_1_as : 22'bz;  // Controlled_Buffer controlled_buffer_5
  not not_15 (not_15_out, and_4_out);
  and and_10 (and_10_out, not_15_out, cpu_dcode_3x8_w_ena_2_o4);
  assign {controlled_buffer_3_out[21], IRe, MARbs, PCoe, PCena, RAMe, RAMs, MARs, IARe, IARs, IRs, R3e, R3s, R2e, R2s, R1e, R1s, R0e, R0s, ALUoe, ALUos, As} = and_10_out ? {{4{lw_satrt_at1_finale_1_as[21]}}, lw_satrt_at1_finale_1_as[17:0]} : 22'bz;  // Controlled_Buffer controlled_buffer_6
  not not_16 (not_16_out, and_4_out);
  and and_11 (and_11_out, not_16_out, cpu_dcode_3x8_w_ena_2_o5);
  assign {controlled_buffer_3_out[21], IRe, MARbs, PCoe, PCena, RAMe, RAMs, MARs, IARe, IARs, IRs, R3e, R3s, R2e, R2s, R1e, R1s, R0e, R0s, ALUoe, ALUos, As} = and_11_out ? {{4{sw_starts_at_1_finale_1_as[21]}}, sw_starts_at_1_finale_1_as[17:0]} : 22'bz;  // Controlled_Buffer controlled_buffer_7
  assign {controlled_buffer_3_out[21], IRe, MARbs, PCoe, PCena, RAMe, RAMs, MARs, IARe, IARs, IRs, R3e, R3s, R2e, R2s, R1e, R1s, R0e, R0s, ALUoe, ALUos, As} = cpu_dcode_3x8_w_ena_2_o6 ? {{4{mov_starts_at_1_finale_1_as[21]}}, mov_starts_at_1_finale_1_as[17:0]} : 22'bz;  // Controlled_Buffer controlled_buffer_8
  assign controlled_buffer_1_out = and_27_out[1] ? ram_1_dout : 8'bz;  // Controlled_Buffer controlled_buffer_9
  _7_Segment_Display u_7_segment_display_1 ();  // open: g, f, a, b, e, d, c, dp
  _7_Segment_Display u_7_segment_display_2 ();  // open: g, f, a, b, e, d, c, dp
  // BCD_to_7_Segment_decoder bcd_to_7_segment_decoder_1: pin names not known
  // BCD_to_7_Segment_decoder bcd_to_7_segment_decoder_2: pin names not known
  // Binary_to_BCD_converter binary_to_bcd_converter_1: pin names not known
  Pull_Resistor pull_resistor_9 (.node({controlled_buffer_3_out[21], IRe, MARbs, PCoe, PCena, RAMe, RAMs, MARs, IARe, IARs, IRs, R3e, R3s, R2e, R2s, R1e, R1s, R0e, R0s, ALUoe, ALUos, As}));
  _7_Segment_Display u_7_segment_display_3 ();  // open: g, f, a, b, e, d, c, dp
  // BCD_to_7_Segment_decoder bcd_to_7_segment_decoder_3: pin names not known
  and and_12 (and_30_out[4], 1'b1, As);
  and and_13 (and_30_out[2], 1'b1, ALUos);
  and and_14 (and_30_out[3], 1'b1, ALUoe);
  and and_15 (and_15_out[0], 1'b1, R0s);
  and and_16 (and_15_out[1], 1'b1, R0e);
  and and_17 (and_15_out[2], 1'b1, R1s);
  and and_18 (and_15_out[3], 1'b1, R1e);
  and and_19 (and_15_out[4], 1'b1, R2s);
  and and_20 (and_15_out[5], 1'b1, R2e);
  and and_21 (and_15_out[6], 1'b1, R3s);
  and and_22 (and_15_out[7], 1'b1, R3e);
  and and_23 (and_32_out[1], 1'b1, IRs);
  and and_24 (and_25_out[5], 1'b1, IARs);
  and and_25 (and_25_out[4], 1'b1, IARe);
  and and_26 (and_31_out[1], 1'b1, MARs);
  and and_27 (and_27_out[0], 1'b1, RAMs);
  and and_28 (and_27_out[1], 1'b1, RAMe);
  and and_29 (and_30_out[1], 1'b1, PCena);
  and and_30 (and_30_out[0], 1'b1, PCoe);
  and and_31 (and_31_out[0], 1'b1, MARbs);
  and and_32 (and_32_out[0], 1'b1, IRe);

  assign MBRd = IARin;
endmodule

module andoraddsub_w_propogation (
  input  [2:0] count,
  input  [3:0] reg_sel,
  output As,
  output ALUos,
  output ALUoe,
  output R0s,
  output R0e,
  output R1s,
  output R1e,
  output R2s,
  output R2e,
  output R3s,
  output R3e,
  output IRs,
  output IARs,
  output IARe,
  output MARs,
  output RAMs,
  output RAMe,
  output PCena,
  output PCoe,
  output MARbs,
  output IRe
);

  wire and_1_out, and_2_out, and_3_out, and_4_out, and_5_out, and_6_out, and_7_out, and_8_out, and_11_out,
       and_12_out, and_13_out, and_14_out, and_16_out, and_17_out, and_18_out, and_19_out, and_21_out,
       and_22_out, and_23_out, and_24_out, and_26_out, and_27_out, and_28_out, and_30_out, and_31_out,
       and_32_out, and_33_out, and_34_out, and_35_out, and_37_out, and_38_out, and_39_out, and_40_out,
       and_41_out, and_42_out, and_43_out, and_44_out, and_45_out, and_46_out, and_47_out, and_48_out,
       and_49_out, and_50_out, and_51_out, and_52_out, not_1_out, not_2_out, not_3_out, not_4_out, not_5_out,
       not_6_out, not_7_out;

  not not_1 (not_1_out, count[2]);
  not not_2 (not_2_out, count[1]);
  not not_3 (not_3_out, count[0]);
  not not_4 (not_4_out, reg_sel[3]);
  not not_5 (not_5_out, reg_sel[2]);
  not not_6 (not_6_out, reg_sel[1]);
  not not_7 (not_7_out, reg_sel[0]);
  and and_1 (and_1_out, not_1_out, count[1], not_3_out, not_5_out, reg_sel[0]);
  and and_2 (and_2_out, not_1_out, count[1], not_3_out, not_4_out, reg_sel[1]);
  and and_3 (and_3_out, not_1_out, count[1], not_3_out, reg_sel[2], not_7_out);
  and and_4 (and_4_out, not_1_out, count[1], not_3_out, reg_sel[3], not_6_out);
  and and_5 (and_5_out, not_1_out, count[1], count[0], not_5_out, reg_sel[0]);
  and and_6 (and_6_out, not_1_out, count[1], count[0], not_4_out, reg_sel[1]);
  and and_7 (and_7_out, not_1_out, count[1], count[0], reg_sel[2], not_7_out);
  and and_8 (and_8_out, not_1_out, count[1], count[0], reg_sel[3], not_6_out);
  and and_9 (ALUoe, count[2], not_2_out, not_3_out);
  and and_10 (R0s, count[2], not_2_out, not_3_out, not_4_out, not_5_out);
  and and_11 (and_11_out, not_1_out, count[1], not_3_out, not_4_out, not_5_out, reg_sel[0]);
  and and_12 (and_12_out, not_1_out, count[1], not_3_out, not_4_out, not_5_out, reg_sel[1]);
  and and_13 (and_13_out, not_1_out, count[1], count[0], reg_sel[2], not_6_out, not_7_out);
  and and_14 (and_14_out, not_1_out, count[1], count[0], reg_sel[3], not_6_out, not_7_out);
  and and_15 (R1s, count[2], not_2_out, not_3_out, not_4_out, reg_sel[2]);
  and and_16 (and_16_out, not_1_out, count[1], count[0], not_5_out, not_6_out, reg_sel[0]);
  and and_17 (and_17_out, not_1_out, count[1], not_3_out, not_4_out, reg_sel[2], not_7_out);
  and and_18 (and_18_out, not_1_out, count[1], not_3_out, not_4_out, reg_sel[2], reg_sel[1]);
  and and_19 (and_19_out, not_1_out, count[1], count[0], reg_sel[3], not_6_out, reg_sel[0]);
  and and_20 (R2s, count[2], not_2_out, not_3_out, reg_sel[3], not_5_out);
  and and_21 (and_21_out, not_1_out, count[1], count[0], not_4_out, reg_sel[1], not_7_out);
  and and_22 (and_22_out, not_1_out, count[1], not_3_out, reg_sel[3], not_5_out, not_6_out);
  and and_23 (and_23_out, not_1_out, count[1], not_3_out, reg_sel[3], not_5_out, reg_sel[0]);
  and and_24 (and_24_out, not_1_out, count[1], count[0], reg_sel[2], reg_sel[1], not_7_out);
  and and_25 (R3s, count[2], not_2_out, not_3_out, reg_sel[3], reg_sel[2]);
  and and_26 (and_26_out, not_1_out, count[1], count[0], reg_sel[1], reg_sel[0]);
  and and_27 (and_27_out, not_1_out, count[1], not_3_out, reg_sel[3], reg_sel[2], not_6_out);
  and and_28 (and_28_out, not_1_out, count[1], not_3_out, reg_sel[3], reg_sel[2], not_7_out);
  and and_29 (IRs, not_1_out, not_2_out, count[0]);
  and and_30 (and_30_out, not_1_out, not_2_out, not_3_out);
  and and_31 (and_31_out, count[2], not_2_out, count[0]);
  and and_32 (and_32_out, not_3_out, not_4_out, not_5_out, not_6_out, not_7_out);
  and and_33 (and_33_out, not_1_out, not_3_out, not_4_out, reg_sel[2], not_6_out, reg_sel[0]);
  and and_34 (and_34_out, not_1_out, not_3_out, reg_sel[3], not_5_out, reg_sel[1], not_7_out);
  and and_35 (and_35_out, not_1_out, not_3_out, reg_sel[3], reg_sel[2], reg_sel[1], reg_sel[0]);
  and and_36 (RAMe, not_1_out, not_2_out, count[0]);
  and and_37 (and_37_out, count[1], not_3_out, not_4_out, not_5_out, not_6_out, not_7_out);
  and and_38 (and_38_out, count[2], not_2_out, not_3_out);
  and and_39 (and_39_out, not_1_out, count[1], not_3_out, not_4_out, reg_sel[2], not_6_out, reg_sel[0]);
  and and_40 (and_40_out, not_1_out, count[1], not_3_out, reg_sel[3], not_5_out, reg_sel[1], not_7_out);
  and and_41 (and_41_out, not_1_out, count[1], reg_sel[3], reg_sel[2], reg_sel[1], reg_sel[0]);
  and and_42 (and_42_out, not_1_out, not_2_out, not_3_out);
  and and_43 (and_43_out, count[2], not_2_out, count[0]);
  and and_44 (and_44_out, not_3_out, not_4_out, not_5_out, not_6_out, not_7_out);
  and and_45 (and_45_out, not_1_out, not_3_out, not_4_out, reg_sel[2], not_6_out, reg_sel[0]);
  and and_46 (and_46_out, not_1_out, not_3_out, reg_sel[3], not_5_out, reg_sel[1], not_7_out);
  and and_47 (and_47_out, not_1_out, not_3_out, reg_sel[3], reg_sel[2], reg_sel[1], reg_sel[0]);
  and and_48 (and_48_out, not_2_out, count[0]);
  and and_49 (and_49_out, count[1], not_3_out, not_4_out, not_5_out, not_6_out, not_7_out);
  and and_50 (and_50_out, not_1_out, count[1], not_3_out, not_4_out, reg_sel[2], not_6_out, reg_sel[0]);
  and and_51 (and_51_out, not_1_out, count[1], not_3_out, reg_sel[3], not_5_out, reg_sel[1], not_7_out);
  and and_52 (and_52_out, not_1_out, count[1], reg_sel[3], reg_sel[2], reg_sel[1], reg_sel[0]);
  or or_1 (As, and_1_out, and_2_out, and_3_out, and_4_out);
  or or_2 (ALUos, and_5_out, and_6_out, and_7_out, and_8_out);
  or or_3 (R0e, and_11_out, and_12_out, and_13_out, and_14_out);
  or or_4 (R1e, and_16_out, and_17_out, and_18_out, and_19_out);
  or or_5 (R2e, and_21_out, and_22_out, and_23_out, and_24_out);
  or or_6 (R3e, and_26_out, and_27_out, and_28_out);
  or or_7 (MARs, and_30_out, and_31_out, and_32_out, and_33_out, and_34_out, and_35_out);
  or or_8 (PCena, and_37_out, and_38_out, and_39_out, and_40_out, and_41_out);
  or or_9 (PCoe, and_42_out, and_43_out, and_44_out, and_45_out, and_46_out, and_47_out);
  or or_10 (IRe, and_48_out, and_49_out, and_50_out, and_51_out, and_52_out);

  assign IARe = 1'b0;
  assign IARs = 1'b0;
  assign MARbs = 1'b0;
  assign RAMs = 1'b0;
endmodule

module LW_satrt_at1_finale (
  input  [2:0] count,
  input  [3:0] op_code,
  output As,
  output ALUos,
  output ALUoe,
  output R0s,
  output R0e,
  output R1s,
  output R1e,
  output R2s,
  output R2e,
  output R3s,
  output R3e,
  output IRs,
  output IARs,
  output IARe,
  output MARs,
  output RAMs,
  output RAMe,
  output PCena
);

  wire and_1_out, and_2_out, and_3_out, and_4_out, and_5_out, and_6_out, and_7_out, and_8_out, and_9_out,
       and_10_out, and_11_out, and_12_out, and_13_out, and_14_out, and_15_out, and_16_out, and_17_out,
       and_18_out, and_19_out, and_20_out, and_21_out, and_22_out, and_23_out, and_24_out, and_25_out,
       and_26_out, and_27_out, and_28_out, and_29_out, and_30_out, not_1_out, not_2_out, not_3_out,
       not_4_out, not_5_out, not_6_out, not_7_out;

  not not_1 (not_1_out, count[2]);
  and and_1 (and_1_out, not_1_out, count[1]);
  and and_2 (and_2_out, not_1_out, count[0]);
  not not_2 (not_2_out, op_code[3]);
  not not_3 (not_3_out, op_code[2]);
  not not_4 (not_4_out, op_code[1]);
  not not_5 (not_5_out, op_code[0]);
  not not_6 (not_6_out, and_1_out);
  not not_7 (not_7_out, and_2_out);
  and and_3 (and_3_out, not_2_out, not_3_out, op_code[0], and_1_out, not_7_out);
  and and_4 (and_4_out, not_2_out, not_3_out, op_code[1], and_1_out, not_7_out);
  and and_5 (and_5_out, op_code[2], not_4_out, not_5_out, not_6_out, and_2_out);
  and and_6 (and_6_out, op_code[3], not_4_out, not_5_out, not_6_out, and_2_out);
  and and_7 (and_7_out, not_2_out, op_code[2], not_5_out, and_1_out, not_7_out);
  and and_8 (and_8_out, not_2_out, op_code[2], op_code[1], and_1_out, not_7_out);
  and and_9 (and_9_out, not_3_out, not_4_out, op_code[0], not_6_out, and_2_out);
  and and_10 (and_10_out, op_code[3], not_4_out, op_code[0], not_6_out, and_2_out);
  and and_11 (and_11_out, op_code[3], not_3_out, not_4_out, and_1_out, not_7_out);
  and and_12 (and_12_out, op_code[3], not_3_out, op_code[0], and_1_out, not_7_out);
  and and_13 (and_13_out, not_2_out, op_code[1], not_5_out, not_6_out, and_2_out);
  and and_14 (and_14_out, op_code[2], op_code[1], not_5_out, not_6_out, and_2_out);
  and and_15 (and_15_out, op_code[3], op_code[2], not_4_out, and_1_out, not_7_out);
  and and_16 (and_16_out, op_code[3], op_code[2], not_5_out, and_1_out, not_7_out);
  and and_17 (and_17_out, not_2_out, op_code[1], op_code[0], not_6_out, and_2_out);
  and and_18 (and_18_out, not_3_out, op_code[1], op_code[0], not_6_out, and_2_out);
  and and_19 (and_19_out, op_code[2], not_5_out, not_6_out, and_2_out);
  and and_20 (and_20_out, op_code[3], not_4_out, not_6_out, and_2_out);
  and and_21 (and_21_out, not_3_out, op_code[0], not_6_out, and_2_out);
  and and_22 (and_22_out, not_2_out, op_code[1], not_6_out, and_2_out);
  and and_23 (and_23_out, op_code[2], not_5_out, not_6_out, and_2_out);
  and and_24 (and_24_out, op_code[3], not_4_out, not_6_out, and_2_out);
  and and_25 (and_25_out, not_3_out, op_code[0], not_6_out, and_2_out);
  and and_26 (and_26_out, not_2_out, op_code[1], not_6_out, and_2_out);
  and and_27 (and_27_out, op_code[2], not_5_out, and_1_out, not_7_out);
  and and_28 (and_28_out, op_code[3], not_4_out, and_1_out, not_7_out);
  and and_29 (and_29_out, not_3_out, op_code[0], and_1_out, not_7_out);
  and and_30 (and_30_out, not_2_out, op_code[1], and_1_out, not_7_out);
  or or_1 (R0s, and_3_out, and_4_out);
  or or_2 (R0e, and_5_out, and_6_out);
  or or_3 (R1s, and_7_out, and_8_out);
  or or_4 (R1e, and_9_out, and_10_out);
  or or_5 (R2s, and_11_out, and_12_out);
  or or_6 (R2e, and_13_out, and_14_out);
  or or_7 (R3s, and_15_out, and_16_out);
  or or_8 (R3e, and_17_out, and_18_out);
  or or_9 (IARs, and_19_out, and_20_out, and_21_out, and_22_out);
  or or_10 (MARs, and_23_out, and_24_out, and_25_out, and_26_out);
  or or_11 (RAMe, and_27_out, and_28_out, and_29_out, and_30_out);

  assign ALUoe = 1'b0;
  assign ALUos = 1'b0;
  assign As = 1'b0;
  assign IARe = 1'b0;
  assign IRs = 1'b0;
  assign PCena = 1'b0;
  assign RAMs = 1'b0;
endmodule

module LOADim_FINAL_WORKING (
  input  [2:0] counter,
  input  [3:0] reg_sel,
  output As,
  output ALUos,
  output ALUoe,
  output R0s,
  output R0e,
  output R1s,
  output R1e,
  output R2s,
  output R2e,
  output R3s,
  output R3e,
  output IRs,
  output IARs,
  output IARe,
  output MARs,
  output RAMs,
  output RAMe,
  output PCena,
  output PCoe,
  output MARbs,
  output IRe,
  output IRRs
);

  wire not_1_out, not_2_out, not_3_out, not_4_out, not_5_out;
  wire [1:0] and_1_out;

  and and_1 (and_1_out[0], reg_sel[0], reg_sel[2]);
  and and_2 (and_1_out[1], reg_sel[1], reg_sel[3]);
  not not_1 (not_1_out, counter[2]);
  not not_2 (not_2_out, counter[1]);
  not not_3 (not_3_out, counter[0]);
  not not_4 (not_4_out, and_1_out[1]);
  not not_5 (not_5_out, and_1_out[0]);
  and and_3 (R0s, not_1_out, counter[1], counter[0], not_4_out, not_5_out);
  and and_4 (R1s, not_1_out, counter[1], counter[0], not_4_out, and_1_out[0]);
  and and_5 (R2s, not_1_out, counter[1], counter[0], and_1_out[1], not_5_out);
  and and_6 (R3s, not_1_out, counter[1], counter[0], and_1_out[1], and_1_out[0]);
  and and_7 (IRs, not_1_out, not_2_out, counter[0]);
  and and_8 (MARs, not_1_out, not_3_out);
  and and_9 (RAMe, not_1_out, counter[0]);
  and and_10 (PCena, not_1_out, counter[0]);
  and and_11 (PCoe, not_1_out, not_3_out);

  assign ALUoe = 1'b0;
  assign ALUos = 1'b0;
  assign As = 1'b0;
  assign IARe = 1'b0;
  assign IARs = 1'b0;
  assign IRe = 1'b1;
  assign IRRs = 1'b0;
  assign MARbs = 1'b0;
  assign R0e = 1'b0;
  assign R1e = 1'b0;
  assign R2e = 1'b0;
  assign R3e = 1'b0;
  assign RAMs = 1'b0;
endmodule

module SW_starts_at_1_finale (
  input  [2:0] count,
  input  [3:0] op_code,
  output As,
  output ALUos,
  output ALUoe,
  output R0s,
  output R0e,
  output R1s,
  output R1e,
  output R2s,
  output R2e,
  output R3s,
  output R3e,
  output IRs,
  output IARs,
  output IARe,
  output MARs,
  output RAMs,
  output RAMe,
  output PCena
);

  wire and_1_out, and_2_out, and_3_out, and_4_out, and_5_out, and_6_out, and_7_out, and_8_out, and_9_out,
       and_10_out, and_11_out, and_12_out, and_13_out, and_14_out, and_15_out, and_16_out, and_17_out,
       and_18_out, and_19_out, and_20_out, and_21_out, and_22_out, and_23_out, and_24_out, and_25_out,
       and_26_out, and_27_out, and_28_out, and_29_out, and_30_out, not_1_out, not_2_out, not_3_out,
       not_4_out, not_5_out, not_6_out, not_7_out;

  not not_1 (not_1_out, count[2]);
  and and_1 (and_1_out, not_1_out, count[1]);
  and and_2 (and_2_out, not_1_out, count[0]);
  not not_2 (not_2_out, op_code[3]);
  not not_3 (not_3_out, op_code[2]);
  not not_4 (not_4_out, op_code[1]);
  not not_5 (not_5_out, op_code[0]);
  not not_6 (not_6_out, and_1_out);
  not not_7 (not_7_out, and_2_out);
  and and_3 (and_3_out, op_code[2], not_4_out, not_5_out, not_6_out, and_2_out);
  and and_4 (and_4_out, op_code[3], not_4_out, not_5_out, not_6_out, and_2_out);
  and and_5 (and_5_out, not_2_out, not_3_out, op_code[0], and_1_out, not_7_out);
  and and_6 (and_6_out, not_2_out, not_3_out, op_code[1], and_1_out, not_7_out);
  and and_7 (and_7_out, not_2_out, op_code[2], not_5_out, and_1_out, not_7_out);
  and and_8 (and_8_out, not_3_out, not_4_out, op_code[0], not_6_out, and_2_out);
  and and_9 (and_9_out, op_code[3], not_4_out, op_code[0], not_6_out, and_2_out);
  and and_10 (and_10_out, not_2_out, op_code[2], op_code[1], and_1_out, not_7_out);
  and and_11 (and_11_out, op_code[3], not_3_out, not_4_out, and_1_out, not_7_out);
  and and_12 (and_12_out, not_2_out, op_code[1], not_5_out, not_6_out, and_2_out);
  and and_13 (and_13_out, op_code[2], op_code[1], not_5_out, not_6_out, and_2_out);
  and and_14 (and_14_out, op_code[3], not_3_out, op_code[0], and_1_out, not_7_out);
  and and_15 (and_15_out, op_code[3], op_code[2], not_4_out, op_code[0], and_1_out, not_7_out);
  and and_16 (and_16_out, op_code[3], op_code[2], op_code[1], not_5_out, and_1_out, not_7_out);
  and and_17 (and_17_out, not_2_out, op_code[1], op_code[0], not_6_out, and_2_out);
  and and_18 (and_18_out, not_3_out, op_code[1], op_code[0], not_6_out, and_2_out);
  and and_19 (and_19_out, op_code[2], not_5_out, not_6_out, and_2_out);
  and and_20 (and_20_out, op_code[3], not_4_out, not_6_out, and_2_out);
  and and_21 (and_21_out, not_3_out, op_code[0], not_6_out, and_2_out);
  and and_22 (and_22_out, not_2_out, op_code[1], not_6_out, and_2_out);
  and and_23 (and_23_out, op_code[2], not_5_out, not_6_out, and_2_out);
  and and_24 (and_24_out, op_code[3], not_4_out, not_6_out, and_2_out);
  and and_25 (and_25_out, not_3_out, op_code[0], not_6_out, and_2_out);
  and and_26 (and_26_out, not_2_out, op_code[1], not_6_out, and_2_out);
  and and_27 (and_27_out, op_code[2], not_5_out, and_1_out, not_7_out);
  and and_28 (and_28_out, op_code[3], not_4_out, and_1_out, not_7_out);
  and and_29 (and_29_out, not_3_out, op_code[0], and_1_out, not_7_out);
  and and_30 (and_30_out, not_2_out, op_code[1], and_1_out, not_7_out);
  or or_1 (R0e, and_3_out, and_4_out, and_5_out, and_6_out);
  or or_2 (R1e, and_7_out, and_8_out, and_9_out, and_10_out);
  or or_3 (R2e, and_11_out, and_12_out, and_13_out, and_14_out);
  or or_4 (R3e, and_15_out, and_16_out, and_17_out, and_18_out);
  or or_5 (IARs, and_19_out, and_20_out, and_21_out, and_22_out);
  or or_6 (MARs, and_23_out, and_24_out, and_25_out, and_26_out);
  or or_7 (RAMs, and_27_out, and_28_out, and_29_out, and_30_out);

  assign ALUoe = 1'b0;
  assign ALUos = 1'b0;
  assign As = 1'b0;
  assign IARe = 1'b0;
  assign IRs = 1'b0;
  assign PCena = 1'b0;
  assign R0s = 1'b0;
  assign R1s = 1'b0;
  assign R2s = 1'b0;
  assign R3s = 1'b0;
  assign RAMe = 1'b0;
endmodule

module SAVEim_FINAL_WORKING (
  input  [2:0] counter,
  input  [3:0] reg_sel,
  output As,
  output ALUos,
  output ALUoe,
  output R0s,
  output R0e,
  output R1s,
  output R1e,
  output R2s,
  output R2e,
  output R3s,
  output R3e,
  output IRs,
  output IARs,
  output IARe,
  output MARs,
  output RAMs,
  output RAMe,
  output PCena,
  output PCoe,
  output MARbs,
  output IRe,
  output IRRs
);

  wire not_1_out, not_2_out, not_3_out, not_4_out, not_5_out;
  wire [1:0] and_1_out;

  and and_1 (and_1_out[0], reg_sel[0], reg_sel[2]);
  and and_2 (and_1_out[1], reg_sel[1], reg_sel[3]);
  not not_1 (not_1_out, counter[2]);
  not not_2 (not_2_out, counter[1]);
  not not_3 (not_3_out, counter[0]);
  not not_4 (not_4_out, and_1_out[1]);
  not not_5 (not_5_out, and_1_out[0]);
  and and_3 (R0e, not_1_out, counter[1], counter[0], not_4_out, not_5_out);
  and and_4 (R1e, not_1_out, counter[1], counter[0], not_4_out, and_1_out[0]);
  and and_5 (R2e, not_1_out, counter[1], counter[0], and_1_out[1], not_5_out);
  and and_6 (R3e, not_1_out, counter[1], counter[0], and_1_out[1], and_1_out[0]);
  and and_7 (IRs, not_1_out, not_2_out, counter[0]);
  and and_8 (MARs, not_1_out, not_3_out);
  and and_9 (RAMs, not_1_out, counter[1], counter[0]);
  and and_10 (RAMe, not_1_out, not_2_out, counter[0]);
  and and_11 (PCena, not_1_out, counter[0]);
  and and_12 (PCoe, not_1_out, not_3_out);

  assign ALUoe = 1'b0;
  assign ALUos = 1'b0;
  assign As = 1'b0;
  assign IARe = 1'b0;
  assign IARs = 1'b0;
  assign IRe = 1'b1;
  assign IRRs = 1'b0;
  assign MARbs = 1'b0;
  assign R0s = 1'b0;
  assign R1s = 1'b0;
  assign R2s = 1'b0;
  assign R3s = 1'b0;
endmodule

module MOV_starts_at_1_finale (
  input  [2:0] count,
  input  [3:0] op_code,
  output As,
  output ALUos,
  output ALUoe,
  output R0s,
  output R0e,
  output R1s,
  output R1e,
  output R2s,
  output R2e,
  output R3s,
  output R3e,
  output IRs,
  output IARs,
  output IARe,
  output MARs,
  output RAMs,
  output RAMe,
  output PCena
);

  wire and_1_out, and_2_out, and_3_out, and_4_out, and_5_out, and_6_out, and_7_out, and_8_out, and_9_out,
       and_10_out, and_11_out, and_12_out, and_13_out, and_14_out, and_15_out, and_16_out, and_17_out,
       not_1_out, not_2_out, not_3_out, not_4_out, not_5_out, not_6_out;

  not not_1 (not_1_out, count[2]);
  not not_2 (not_2_out, count[1]);
  and and_1 (and_1_out, not_1_out, not_2_out, count[0]);
  not not_3 (not_3_out, op_code[3]);
  not not_4 (not_4_out, op_code[2]);
  not not_5 (not_5_out, op_code[1]);
  not not_6 (not_6_out, op_code[0]);
  and and_2 (and_2_out, not_3_out, not_4_out, op_code[0], and_1_out);
  and and_3 (and_3_out, not_3_out, not_4_out, op_code[1], and_1_out);
  and and_4 (and_4_out, op_code[3], not_5_out, not_6_out, and_1_out);
  and and_5 (and_5_out, op_code[2], not_5_out, not_6_out, and_1_out);
  and and_6 (and_6_out, not_3_out, op_code[2], not_6_out, and_1_out);
  and and_7 (and_7_out, not_3_out, op_code[2], op_code[1], and_1_out);
  and and_8 (and_8_out, not_4_out, not_5_out, op_code[0], and_1_out);
  and and_9 (and_9_out, op_code[3], not_5_out, op_code[0], and_1_out);
  and and_10 (and_10_out, op_code[3], not_4_out, not_5_out, and_1_out);
  and and_11 (and_11_out, op_code[3], not_4_out, op_code[0], and_1_out);
  and and_12 (and_12_out, not_3_out, op_code[1], not_6_out, and_1_out);
  and and_13 (and_13_out, op_code[2], op_code[1], not_6_out, and_1_out);
  and and_14 (and_14_out, op_code[3], op_code[2], not_5_out, and_1_out);
  and and_15 (and_15_out, op_code[3], op_code[2], not_6_out, and_1_out);
  and and_16 (and_16_out, not_4_out, op_code[1], op_code[0], and_1_out);
  and and_17 (and_17_out, not_3_out, op_code[1], op_code[0], and_1_out);
  or or_1 (R0s, and_2_out, and_3_out);
  or or_2 (R0e, and_4_out, and_5_out);
  or or_3 (R1s, and_6_out, and_7_out);
  or or_4 (R1e, and_8_out, and_9_out);
  or or_5 (R2s, and_10_out, and_11_out);
  or or_6 (R2e, and_12_out, and_13_out);
  or or_7 (R3s, and_14_out, and_15_out);
  or or_8 (R3e, and_16_out, and_17_out);

  assign ALUoe = 1'b0;
  assign ALUos = 1'b0;
  assign As = 1'b0;
  assign IARe = 1'b0;
  assign IARs = 1'b0;
  assign IRs = 1'b0;
  assign MARs = 1'b0;
  assign PCena = 1'b0;
  assign RAMe = 1'b0;
  assign RAMs = 1'b0;
endmodule

module FourBitAdder (
  input  [3:0] A,
  input  [3:0] B,
  input  Carry_in,
  output [3:0] Sum,
  output Carry_out
);

  wire and_1_out, and_2_out, and_3_out, and_4_out, and_5_out, and_6_out, and_7_out, and_8_out, or_1_out,
       or_2_out, or_3_out, xor_1_out, xor_2_out, xor_3_out, xor_4_out;

  xor xor_1 (xor_1_out, A[0], B[0]);
  and and_1 (and_1_out, A[0], B[0]);
  xor xor_2 (xor_2_out, A[1], B[1]);
  and and_2 (and_2_out, A[1], B[1]);
  xor xor_3 (xor_3_out, A[2], B[2]);
  and and_3 (and_3_out, A[2], B[2]);
  xor xor_4 (xor_4_out, A[3], B[3]);
  and and_4 (and_4_out, A[3], B[3]);
  xor xor_5 (Sum[0], xor_1_out, Carry_in);
  and and_5 (and_5_out, xor_1_out, Carry_in);
  xor xor_6 (Sum[1], xor_2_out, or_1_out);
  and and_6 (and_6_out, xor_2_out, or_1_out);
  xor xor_7 (Sum[2], xor_3_out, or_2_out);
  and and_7 (and_7_out, xor_3_out, or_2_out);
  xor xor_8 (Sum[3], xor_4_out, or_3_out);
  and and_8 (and_8_out, xor_4_out, or_3_out);
  or or_1 (or_1_out, and_1_out, and_5_out);
  or or_2 (or_2_out, and_2_out, and_6_out);
  or or_3 (or_3_out, and_3_out, and_7_out);
  or or_4 (Carry_out, and_4_out, and_8_out);
endmodule

module EightBitAddSub (
  input  [7:0] num1,
  input  [7:0] num2,
  input  subt,
  input  C_in,
  output [7:0] Result,
  output C_out
);

  wire and_1_out, fourbitadder_1_carry_out, not_1_out, or_1_out;
  wire [3:0] xor_1_out, xor_5_out;

  // Probe on num1
  Pull_Resistor #(.pull(1)) pull_resistor_1 (.node(num1));
  // Probe on num2
  xor xor_1 (xor_1_out[0], num2[0], subt);
  xor xor_2 (xor_1_out[1], num2[1], subt);
  xor xor_3 (xor_1_out[2], num2[2], subt);
  xor xor_4 (xor_1_out[3], num2[3], subt);
  xor xor_5 (xor_5_out[0], num2[4], subt);
  xor xor_6 (xor_5_out[1], num2[5], subt);
  xor xor_7 (xor_5_out[2], num2[6], subt);
  xor xor_8 (xor_5_out[3], num2[7], subt);
  or or_1 (or_1_out, subt, C_in);
  // Probe on and_1_out
  not not_1 (not_1_out, C_out);
  and and_1 (and_1_out, subt, not_1_out);
  FourBitAdder fourbitadder_1 (
    .A(num1[3:0]), .B(xor_1_out), .Carry_in(or_1_out), .Sum(Result[3:0]), .Carry_out(fourbitadder_1_carry_out));
  FourBitAdder fourbitadder_2 (
    .A(num1[7:4]), .B(xor_5_out), .Carry_in(fourbitadder_1_carry_out), .Sum(Result[7:4]), .Carry_out(C_out));
  // Probe on Result
endmodule

module CPU_DCODE_3x8_w_ena (
  input  enable,
  input  [2:0] Sel,
  output O0,
  output O1,
  output O2,
  output O3,
  output O4,
  output O5,
  output O6,
  output O7
);

  wire and_1_out, and_2_out, and_3_out, and_4_out, and_5_out, and_6_out, and_7_out, and_8_out, not_1_out,
       not_2_out, not_3_out, not_4_out, not_5_out, not_6_out, not_7_out, not_8_out, not_9_out, not_10_out,
       not_11_out, not_12_out;

  not not_1 (not_1_out, Sel[0]);
  not not_2 (not_2_out, Sel[1]);
  not not_3 (not_3_out, Sel[2]);
  not not_4 (not_4_out, Sel[1]);
  not not_5 (not_5_out, Sel[2]);
  not not_6 (not_6_out, Sel[0]);
  not not_7 (not_7_out, Sel[2]);
  not not_8 (not_8_out, Sel[2]);
  not not_9 (not_9_out, Sel[0]);
  not not_10 (not_10_out, Sel[1]);
  not not_11 (not_11_out, Sel[1]);
  not not_12 (not_12_out, Sel[0]);
  and and_1 (and_1_out, not_1_out, not_2_out, not_3_out);
  and and_2 (and_2_out, Sel[0], not_4_out, not_5_out);
  and and_3 (and_3_out, not_6_out, Sel[1], not_7_out);
  and and_4 (and_4_out, Sel[0], Sel[1], not_8_out);
  and and_5 (and_5_out, not_9_out, not_10_out, Sel[2]);
  and and_6 (and_6_out, Sel[0], not_11_out, Sel[2]);
  and and_7 (and_7_out, not_12_out, Sel[1], Sel[2]);
  and and_8 (and_8_out, Sel[0], Sel[1], Sel[2]);
  and and_9 (O0, and_1_out, enable);
  and and_10 (O1, and_2_out, enable);
  and and_11 (O2, and_3_out, enable);
  and and_12 (O3, and_4_out, enable);
  and and_13 (O4, and_5_out, enable);
  and and_14 (O5, and_6_out, enable);
  and and_15 (O6, and_7_out, enable);
  and and_16 (O7, and_8_out, enable);
endmodule

module AND_8 (
  input  [7:0] in_1,
  input  [7:0] in_2,
  output [7:0] out_3
);

  and and_1 (out_3[7], in_1[7], in_2[7]);
  and and_2 (out_3[6], in_1[6], in_2[6]);
  and and_3 (out_3[5], in_1[5], in_2[5]);
  and and_4 (out_3[4], in_1[4], in_2[4]);
  and and_5 (out_3[3], in_1[3], in_2[3]);
  and and_6 (out_3[2], in_1[2], in_2[2]);
  and and_7 (out_3[1], in_1[1], in_2[1]);
  and and_8 (out_3[0], in_1[0], in_2[0]);
endmodule

module XOR_8 (
  input  [7:0] in_1,
  input  [7:0] in_2,
  output [7:0] out_3
);

  xor xor_1 (out_3[7], in_1[7], in_2[7]);
  xor xor_2 (out_3[6], in_1[6], in_2[6]);
  xor xor_3 (out_3[5], in_1[5], in_2[5]);
  xor xor_4 (out_3[4], in_1[4], in_2[4]);
  xor xor_5 (out_3[3], in_1[3], in_2[3]);
  xor xor_6 (out_3[2], in_1[2], in_2[2]);
  xor xor_7 (out_3[1], in_1[1], in_2[1]);
  xor xor_8 (out_3[0], in_1[0], in_2[0]);
endmodule

module OR_8 (
  input  [7:0] in_1,
  input  [7:0] in_2,
  output [7:0] out_3
);

  or or_1 (out_3[7], in_1[7], in_2[7]);
  or or_2 (out_3[6], in_1[6], in_2[6]);
  or or_3 (out_3[5], in_1[5], in_2[5]);
  or or_4 (out_3[4], in_1[4], in_2[4]);
  or or_5 (out_3[3], in_1[3], in_2[3]);
  or or_6 (out_3[2], in_1[2], in_2[2]);
  or or_7 (out_3[1], in_1[1], in_2[1]);
  or or_8 (out_3[0], in_1[0], in_2[0]);
endmodule

module Comparator_8 (
  input  [7:0] B,
  input  [7:0] A,
  output Equal,
  output A_Greater,
  output B_Greater
);

  wire and_1_out, and_2_out, and_3_out, and_4_out, and_5_out, and_6_out, and_7_out, and_8_out, and_9_out,
       and_10_out, and_11_out, and_12_out, and_13_out, and_14_out, and_15_out, and_16_out, and_17_out,
       and_18_out, and_19_out, and_20_out, and_21_out, and_22_out, and_23_out, and_24_out, and_25_out,
       and_26_out, and_27_out, and_28_out, and_29_out, and_30_out, nor_1_out, nor_2_out, nor_3_out,
       nor_4_out, nor_5_out, nor_6_out, nor_7_out, nor_8_out, not_1_out, not_2_out, not_3_out, not_4_out,
       not_5_out, not_6_out, not_7_out, not_8_out, not_9_out, not_10_out, not_11_out, not_12_out, not_13_out,
       not_14_out, not_15_out, not_16_out;

  not not_1 (not_1_out, A[0]);
  not not_2 (not_2_out, B[0]);
  not not_3 (not_3_out, A[1]);
  not not_4 (not_4_out, B[1]);
  not not_5 (not_5_out, A[2]);
  not not_6 (not_6_out, B[2]);
  not not_7 (not_7_out, A[3]);
  not not_8 (not_8_out, B[3]);
  not not_9 (not_9_out, A[4]);
  not not_10 (not_10_out, B[4]);
  not not_11 (not_11_out, A[5]);
  not not_12 (not_12_out, B[5]);
  not not_13 (not_13_out, A[6]);
  not not_14 (not_14_out, B[6]);
  not not_15 (not_15_out, A[7]);
  not not_16 (not_16_out, B[7]);
  and and_1 (and_1_out, not_1_out, B[0]);
  and and_2 (and_2_out, A[0], not_2_out);
  and and_3 (and_3_out, not_3_out, B[1]);
  and and_4 (and_4_out, A[1], not_4_out);
  and and_5 (and_5_out, not_5_out, B[2]);
  and and_6 (and_6_out, A[2], not_6_out);
  and and_7 (and_7_out, not_7_out, B[3]);
  and and_8 (and_8_out, A[3], not_8_out);
  and and_9 (and_9_out, not_9_out, B[4]);
  and and_10 (and_10_out, A[4], not_10_out);
  and and_11 (and_11_out, not_11_out, B[5]);
  and and_12 (and_12_out, A[5], not_12_out);
  and and_13 (and_13_out, not_13_out, B[6]);
  and and_14 (and_14_out, A[6], not_14_out);
  and and_15 (and_15_out, not_15_out, B[7]);
  and and_16 (and_16_out, A[7], not_16_out);
  nor nor_1 (nor_1_out, and_1_out, and_2_out);
  nor nor_2 (nor_2_out, and_3_out, and_4_out);
  nor nor_3 (nor_3_out, and_5_out, and_6_out);
  nor nor_4 (nor_4_out, and_7_out, and_8_out);
  nor nor_5 (nor_5_out, and_9_out, and_10_out);
  nor nor_6 (nor_6_out, and_11_out, and_12_out);
  nor nor_7 (nor_7_out, and_13_out, and_14_out);
  nor nor_8 (nor_8_out, and_15_out, and_16_out);
  and and_17 (and_17_out, nor_8_out, nor_7_out, nor_6_out, nor_5_out, nor_4_out, nor_3_out, nor_2_out, and_1_out);
  and and_18 (and_18_out, and_2_out, nor_2_out, nor_3_out, nor_4_out, nor_5_out, nor_6_out, nor_7_out, nor_8_out);
  and and_19 (and_19_out, nor_8_out, nor_7_out, nor_6_out, nor_5_out, nor_4_out, nor_3_out, and_3_out);
  and and_20 (and_20_out, and_4_out, nor_3_out, nor_4_out, nor_5_out, nor_6_out, nor_7_out, nor_8_out);
  and and_21 (and_21_out, nor_8_out, nor_7_out, nor_6_out, nor_5_out, nor_4_out, and_5_out);
  and and_22 (and_22_out, and_6_out, nor_4_out, nor_5_out, nor_6_out, nor_7_out, nor_8_out);
  and and_23 (and_23_out, nor_8_out, nor_7_out, nor_6_out, nor_5_out, and_7_out);
  and and_24 (and_24_out, and_8_out, nor_5_out, nor_6_out, nor_7_out, nor_8_out);
  and and_25 (and_25_out, nor_8_out, nor_7_out, nor_6_out, and_9_out);
  and and_26 (and_26_out, and_10_out, nor_6_out, nor_7_out, nor_8_out);
  and and_27 (and_27_out, nor_8_out, nor_7_out, and_11_out);
  and and_28 (and_28_out, and_12_out, nor_7_out, nor_8_out);
  and and_29 (and_29_out, nor_8_out, and_13_out);
  and and_30 (and_30_out, and_14_out, nor_8_out);
  and and_31 (Equal, nor_1_out, nor_2_out, nor_3_out, nor_4_out, nor_5_out, nor_6_out, nor_7_out, nor_8_out);
  or or_1 (A_Greater, and_18_out, and_20_out, and_22_out, and_24_out, and_26_out, and_28_out, and_30_out, and_16_out);
  or or_2 (B_Greater, and_17_out, and_19_out, and_21_out, and_23_out, and_25_out, and_27_out, and_29_out, and_15_out);
endmodule

module MUX_4x1_8bit (
  input  [1:0] Sel,
  input  [7:0] A,
  input  [7:0] B,
  input  [7:0] C,
  input  [7:0] D,
  output [7:0] O
);

  wire [7:0] and_1_out, and_2_out, and_3_out, and_4_out, not_1_out, not_2_out, not_3_out, not_4_out;

  assign not_1_out = ~{8{Sel[0]}};  // NOT_Gate not_1, 8 bits wide
  assign not_2_out = ~{8{Sel[1]}};  // NOT_Gate not_2, 8 bits wide
  assign not_3_out = ~{8{Sel[1]}};  // NOT_Gate not_3, 8 bits wide
  assign not_4_out = ~{8{Sel[0]}};  // NOT_Gate not_4, 8 bits wide
  assign and_1_out = not_1_out & not_2_out & A;  // AND_Gate and_1, 8 bits wide
  assign and_2_out = {8{Sel[0]}} & not_3_out & B;  // AND_Gate and_2, 8 bits wide
  assign and_3_out = not_4_out & {8{Sel[1]}} & C;  // AND_Gate and_3, 8 bits wide
  assign and_4_out = {8{Sel[0]}} & {8{Sel[1]}} & D;  // AND_Gate and_4, 8 bits wide
  assign O = and_1_out | and_2_out | and_3_out | and_4_out;  // OR_Gate or_1, 8 bits wide
endmodule

module MUX_2x1_8bit (
  input  sel,
  input  [7:0] A,
  input  [7:0] B,
  output [7:0] O
);

  wire [7:0] and_1_out, and_2_out, not_1_out;

  assign not_1_out = ~{8{sel}};  // NOT_Gate not_1, 8 bits wide
  assign and_1_out = not_1_out & A;  // AND_Gate and_1, 8 bits wide
  assign and_2_out = {8{sel}} & B;  // AND_Gate and_2, 8 bits wide
  assign O = and_1_out | and_2_out;  // OR_Gate or_1, 8 bits wide
endmodule

module MUX_8x1_8bit (
  input  [2:0] sel,
  input  [7:0] A,
  input  [7:0] B,
  input  [7:0] C,
  input  [7:0] D,
  input  [7:0] E,
  input  [7:0] F,
  input  [7:0] G,
  input  [7:0] H,
  output [7:0] O
);

  wire [7:0] and_1_out, and_2_out, and_3_out, and_4_out, and_5_out, and_6_out, and_7_out, and_8_out,
       not_1_out, not_2_out, not_3_out, not_4_out, not_5_out, not_6_out, not_7_out, not_8_out, not_9_out,
       not_10_out, not_11_out, not_12_out;

  assign not_1_out = ~{8{sel[0]}};  // NOT_Gate not_1, 8 bits wide
  assign not_2_out = ~{8{sel[1]}};  // NOT_Gate not_2, 8 bits wide
  assign not_3_out = ~{8{sel[2]}};  // NOT_Gate not_3, 8 bits wide
  assign not_4_out = ~{8{sel[1]}};  // NOT_Gate not_4, 8 bits wide
  assign not_5_out = ~{8{sel[2]}};  // NOT_Gate not_5, 8 bits wide
  assign not_6_out = ~{8{sel[0]}};  // NOT_Gate not_6, 8 bits wide
  assign not_7_out = ~{8{sel[2]}};  // NOT_Gate not_7, 8 bits wide
  assign not_8_out = ~{8{sel[2]}};  // NOT_Gate not_8, 8 bits wide
  assign not_9_out = ~{8{sel[0]}};  // NOT_Gate not_9, 8 bits wide
  assign not_10_out = ~{8{sel[1]}};  // NOT_Gate not_10, 8 bits wide
  assign not_11_out = ~{8{sel[1]}};  // NOT_Gate not_11, 8 bits wide
  assign not_12_out = ~{8{sel[0]}};  // NOT_Gate not_12, 8 bits wide
  assign and_1_out = not_1_out & not_2_out & not_3_out & A;  // AND_Gate and_1, 8 bits wide
  assign and_2_out = {8{sel[0]}} & not_4_out & not_5_out & B;  // AND_Gate and_2, 8 bits wide
  assign and_3_out = not_6_out & {8{sel[1]}} & not_7_out & C;  // AND_Gate and_3, 8 bits wide
  assign and_4_out = {8{sel[0]}} & {8{sel[1]}} & not_8_out & D;  // AND_Gate and_4, 8 bits wide
  assign and_5_out = not_9_out & not_10_out & {8{sel[2]}} & E;  // AND_Gate and_5, 8 bits wide
  assign and_6_out = {8{sel[0]}} & not_11_out & {8{sel[2]}} & F;  // AND_Gate and_6, 8 bits wide
  assign and_7_out = not_12_out & {8{sel[1]}} & {8{sel[2]}} & G;  // AND_Gate and_7, 8 bits wide
  assign and_8_out = {8{sel[0]}} & {8{sel[1]}} & {8{sel[2]}} & H;  // AND_Gate and_8, 8 bits wide
  assign O = and_1_out | and_2_out | and_3_out | and_4_out | and_5_out | and_6_out | and_7_out | and_8_out;  // OR_Gate or_1, 8 bits wide
endmodule

module L_shift (
  input  [7:0] I,
  output [7:0] O,
  output C_out
);


  assign C_out = I[7];
  assign O = {I[6:0], 1'b0};
endmodule

module R_shift (
  input  [7:0] I,
  output C_out,
  output [7:0] O
);


  assign C_out = I[0];
  assign O = {1'b0, I[7:1]};
endmodule

module PC (
  input  en,
  input  clk,
  input  clr,
  output [7:0] O
);

  wire and_1_out, and_2_out, and_3_out, and_4_out, and_5_out, and_6_out, clock_2_out, clock_3_out,
       clock_4_out, clock_5_out, clock_6_out, clock_7_out, comparator_8_1_a_greater,
       digital_oscilloscope_1_p2, digital_oscilloscope_1_p3, digital_oscilloscope_1_p4, j_k_ff_1_q,
       j_k_ff_2_q, j_k_ff_3_q, mclk_out, nor_1_out, nor_2_out, nor_3_out, nor_4_out, nor_5_out, nor_6_out,
       or_1_out, pull_resistor_1_node, pull_resistor_2_node, pull_resistor_3_node, pull_resistor_4_node,
       pull_resistor_5_node, pull_resistor_6_node, pull_resistor_7_node, pull_resistor_8_node,
       pull_resistor_9_node, pull_resistor_10_node, pull_resistor_11_node, pull_resistor_12_node;
  wire [7:0] eightbitaddsub_1_result;

  Register register_1 (.D(eightbitaddsub_1_result), .en(en), .clk(mclk_out), .Q(O), .clr(or_1_out));
  or or_1 (or_1_out, comparator_8_1_a_greater, clr);
  Comparator_8 comparator_8_1 (.A(O), .B(8'h7), .A_Greater(comparator_8_1_a_greater));  // open: B_Greater, Equal
  Pull_Resistor pull_resistor_1 (.node(pull_resistor_1_node));
  Comparator_8 comparator_8_2 (.A(O), .B(8'h3), .A_Greater(pull_resistor_1_node));  // open: B_Greater, Equal
  Pull_Resistor pull_resistor_2 (.node(pull_resistor_2_node));
  Comparator_8 comparator_8_3 (.A(O), .B(8'h2), .Equal(pull_resistor_2_node));  // open: B_Greater, A_Greater
  Pull_Resistor pull_resistor_3 (.node(pull_resistor_3_node));
  Comparator_8 comparator_8_4 (.A(O), .B(8'h5), .A_Greater(pull_resistor_3_node));  // open: B_Greater, Equal
  Pull_Resistor pull_resistor_4 (.node(pull_resistor_4_node));
  Comparator_8 comparator_8_5 (.A(O), .B(8'h8), .Equal(pull_resistor_4_node));  // open: B_Greater, A_Greater
  Pull_Resistor pull_resistor_5 (.node(pull_resistor_5_node));
  Comparator_8 comparator_8_6 (.A(O), .B(8'h5), .A_Greater(pull_resistor_5_node));  // open: B_Greater, Equal
  Pull_Resistor pull_resistor_6 (.node(pull_resistor_6_node));
  Comparator_8 comparator_8_7 (.A(O), .B(8'h2), .Equal(pull_resistor_6_node));  // open: B_Greater, A_Greater
  Pull_Resistor pull_resistor_7 (.node(pull_resistor_7_node));
  Comparator_8 comparator_8_8 (.A(O), .B(8'h2), .A_Greater(pull_resistor_7_node));  // open: B_Greater, Equal
  Pull_Resistor pull_resistor_8 (.node(pull_resistor_8_node));
  Comparator_8 comparator_8_9 (.A(O), .B(8'h1), .Equal(pull_resistor_8_node));  // open: B_Greater, A_Greater
  Pull_Resistor pull_resistor_9 (.node(pull_resistor_9_node));
  Comparator_8 comparator_8_10 (.A(O), .B(8'h4), .A_Greater(pull_resistor_9_node));  // open: B_Greater, Equal
  Pull_Resistor pull_resistor_10 (.node(pull_resistor_10_node));
  Comparator_8 comparator_8_11 (.A(O), .B(8'h7), .Equal(pull_resistor_10_node));  // open: B_Greater, A_Greater
  Pull_Resistor pull_resistor_11 (.node(pull_resistor_11_node));
  Comparator_8 comparator_8_12 (.A(O), .B(8'h4), .A_Greater(pull_resistor_11_node));  // open: B_Greater, Equal
  Pull_Resistor pull_resistor_12 (.node(pull_resistor_12_node));
  Comparator_8 comparator_8_13 (.A(O), .B(8'h1), .Equal(pull_resistor_12_node));  // open: B_Greater, A_Greater
  and and_1 (and_1_out, pull_resistor_1_node, mclk_out);
  and and_2 (and_2_out, mclk_out, pull_resistor_2_node);
  and and_3 (and_3_out, pull_resistor_3_node, mclk_out);
  and and_4 (and_4_out, mclk_out, pull_resistor_4_node);
  and and_5 (and_5_out, pull_resistor_5_node, mclk_out);
  and and_6 (and_6_out, mclk_out, pull_resistor_6_node);
  J_K_Flip_Flop j_k_ff_1 (
    .J(pull_resistor_7_node), .K(pull_resistor_8_node), .clk(mclk_out), .Q(j_k_ff_1_q));  // open: Qn, preset, reset
  J_K_Flip_Flop j_k_ff_2 (
    .J(pull_resistor_9_node), .K(pull_resistor_10_node), .clk(mclk_out), .Q(j_k_ff_2_q));  // open: Qn, preset, reset
  J_K_Flip_Flop j_k_ff_3 (
    .J(pull_resistor_11_node), .K(pull_resistor_12_node), .clk(mclk_out), .Q(j_k_ff_3_q));  // open: Qn, preset, reset
  EightBitAddSub eightbitaddsub_1 (
    .num1(O), .subt(1'b0), .C_in(1'b1), .Result(eightbitaddsub_1_result));  // open: num2, C_out
  nor nor_1 (nor_1_out, and_1_out, nor_2_out);
  nor nor_2 (nor_2_out, nor_1_out, and_2_out);
  nor nor_3 (nor_3_out, and_3_out, nor_4_out);
  nor nor_4 (nor_4_out, nor_3_out, and_4_out);
  nor nor_5 (nor_5_out, and_5_out, nor_6_out);
  nor nor_6 (nor_6_out, nor_5_out, and_6_out);
  Clock mclk (.out(mclk_out));
  // Digital_Oscilloscope #(.nState(20)) digital_oscilloscope_1: pin names not known; wires that end beside it: mclk_out, digital_oscilloscope_1_p2, digital_oscilloscope_1_p3, digital_oscilloscope_1_p4, nor_2_out, nor_4_out, nor_6_out
  Clock #(.highDuration(3), .phaseOffset(1)) ena (.out(digital_oscilloscope_1_p2));
  Clock #(.lowDuration(3), .phaseOffset(2)) set (.out(digital_oscilloscope_1_p3));
  Clock #(.highDuration(2), .lowDuration(2), .phaseOffset(1)) clock_1 (.out(digital_oscilloscope_1_p4));
  Clock #(.highDuration(12), .lowDuration(4), .phaseOffset(1)) clock_2 (.out(clock_2_out));
  Clock #(.highDuration(4), .lowDuration(12), .phaseOffset(5)) clock_3 (.out(clock_3_out));
  Clock #(.highDuration(8), .lowDuration(8), .phaseOffset(1)) clock_4 (.out(clock_4_out));
  Clock #(.highDuration(6), .lowDuration(2), .phaseOffset(1)) clock_5 (.out(clock_5_out));
  Clock #(.highDuration(2), .lowDuration(6), .phaseOffset(3)) clock_6 (.out(clock_6_out));
  Clock #(.highDuration(4), .lowDuration(4), .phaseOffset(1)) clock_7 (.out(clock_7_out));
endmodule

module mem1_noclr (
  input  s,
  input  e,
  output o
);

  wire and_1_out, and_2_out, nor_1_out, not_1_out;

  Pull_Resistor pull_resistor_1 (.node(s));
  Pull_Resistor pull_resistor_2 (.node(e));
  not not_1 (not_1_out, s);
  and and_1 (and_1_out, s, e);
  and and_2 (and_2_out, e, not_1_out);
  nor nor_1 (nor_1_out, and_1_out, o);
  nor nor_2 (o, nor_1_out, and_2_out);
  Pull_Resistor pull_resistor_3 (.node(nor_1_out));
endmodule

module mem_1 (
  input  s,
  input  e,
  input  clr,
  output o
);

  wire nand_1_out, nand_2_out, nand_4_out, not_1_out, xor_1_out;

  not not_1 (not_1_out, s);
  nand nand_1 (nand_1_out, s, e);
  nand nand_2 (nand_2_out, e, not_1_out);
  xor xor_1 (xor_1_out, nand_2_out, clr);
  nand nand_3 (o, nand_1_out, nand_4_out);
  nand nand_4 (nand_4_out, o, xor_1_out);
endmodule

module mem_8 (
  input  [7:0] s,
  input  e,
  input  clr,
  output [7:0] o
);

  mem_1 mem_1_1 (.e(e), .clr(clr), .s(s[0]), .o(o[0]));
  mem_1 mem_1_2 (.e(e), .clr(clr), .s(s[1]), .o(o[1]));
  mem_1 mem_1_3 (.e(e), .clr(clr), .s(s[2]), .o(o[2]));
  mem_1 mem_1_4 (.e(e), .clr(clr), .s(s[3]), .o(o[3]));
  mem_1 mem_1_5 (.e(e), .clr(clr), .s(s[4]), .o(o[4]));
  mem_1 mem_1_6 (.e(e), .clr(clr), .s(s[5]), .o(o[5]));
  mem_1 mem_1_7 (.e(e), .clr(clr), .s(s[6]), .o(o[6]));
  mem_1 mem_1_8 (.e(e), .clr(clr), .s(s[7]), .o(o[7]));
endmodule

module ena_8 (
  input  [7:0] i,
  input  e,
  output [7:0] o
);

  wire [7:0] and_1_out;

  and and_1 (and_1_out[0], i[0], e);
  and and_2 (and_1_out[1], i[1], e);
  and and_3 (and_1_out[2], i[2], e);
  and and_4 (and_1_out[3], i[3], e);
  and and_5 (and_1_out[4], i[4], e);
  and and_6 (and_1_out[5], i[5], e);
  and and_7 (and_1_out[6], i[6], e);
  and and_8 (and_1_out[7], i[7], e);
  assign o = e ? and_1_out : 8'bz;  // Controlled_Buffer controlled_buffer_1
endmodule

module reg_8 (
  input  [7:0] i,
  input  s,
  input  e,
  input  clr,
  output [7:0] o,
  output [7:0] ireg
);

  wire [7:0] ena_8_1_o;

  mem_8 mem_8_1 (.e(s), .s(i), .clr(clr), .o(ireg));
  ena_8 ena_8_1 (.i(ireg), .e(e), .o(ena_8_1_o));
  assign o = e ? ena_8_1_o : 8'bz;  // Controlled_Buffer controlled_buffer_1
endmodule

module ena_1 (
  input  i,
  input  e,
  output o
);

  and and_1 (o, i, e);
endmodule

module reg_1 (
  input  i,
  input  s,
  input  e,
  input  clr,
  output o,
  output ireg
);

  wire ena_1_1_o;

  mem_1 mem_1_1 (.e(s), .clr(clr), .s(i), .o(ireg));
  assign o = e ? ena_1_1_o : 1'bz;  // Controlled_Buffer controlled_buffer_1
  ena_1 ena_1_1 (.i(ireg), .e(e), .o(ena_1_1_o));
  Pull_Resistor pull_resistor_1 (.node(o));
endmodule

module ram_reg_1 (
  input  i,
  input  x,
  input  y,
  input  set,
  input  ena,
  input  clr,
  output mem,
  output o
);

  wire and_1_out, and_2_out, reg_1_1_o;

  and and_1 (and_1_out, x, y, set);
  and and_2 (and_2_out, x, y, ena);
  assign o = and_2_out ? reg_1_1_o : 1'bz;  // Controlled_Buffer controlled_buffer_1
  reg_1 reg_1_1 (.i(i), .s(and_1_out), .e(and_2_out), .clr(clr), .o(reg_1_1_o), .ireg(mem));
  Pull_Resistor pull_resistor_1 (.node(o));
endmodule

module rem_reg_8 (
  input  [7:0] i,
  input  y,
  input  x,
  input  set,
  input  ena,
  input  clr,
  output [7:0] o,
  output [7:0] ireg
);

  wire and_1_out;
  wire [7:0] ram_reg_1_1_o;

  and and_1 (and_1_out, y, x, ena);
  ram_reg_1 ram_reg_1_1 (.i(i[0]), .x(x), .y(y), .set(set), .ena(ena), .clr(clr), .mem(ireg[0]), .o(ram_reg_1_1_o[0]));
  ram_reg_1 ram_reg_1_2 (.i(i[1]), .x(x), .y(y), .set(set), .ena(ena), .clr(clr), .mem(ireg[1]), .o(ram_reg_1_1_o[1]));
  ram_reg_1 ram_reg_1_3 (.i(i[2]), .x(x), .y(y), .set(set), .ena(ena), .clr(clr), .mem(ireg[2]), .o(ram_reg_1_1_o[2]));
  ram_reg_1 ram_reg_1_4 (.i(i[3]), .x(x), .y(y), .set(set), .ena(ena), .clr(clr), .mem(ireg[3]), .o(ram_reg_1_1_o[3]));
  ram_reg_1 ram_reg_1_5 (.i(i[4]), .x(x), .y(y), .set(set), .ena(ena), .clr(clr), .mem(ireg[4]), .o(ram_reg_1_1_o[4]));
  ram_reg_1 ram_reg_1_6 (.i(i[5]), .x(x), .y(y), .set(set), .ena(ena), .clr(clr), .mem(ireg[5]), .o(ram_reg_1_1_o[5]));
  ram_reg_1 ram_reg_1_7 (.i(i[6]), .x(x), .y(y), .set(set), .ena(ena), .clr(clr), .mem(ireg[6]), .o(ram_reg_1_1_o[6]));
  ram_reg_1 ram_reg_1_8 (.i(i[7]), .x(x), .y(y), .set(set), .ena(ena), .clr(clr), .mem(ireg[7]), .o(ram_reg_1_1_o[7]));
  assign o = and_1_out ? ram_reg_1_1_o : 8'bz;  // Controlled_Buffer controlled_buffer_1
endmodule

module RAM_16B_8b (
  input  [3:0] addr,
  input  [7:0] I,
  input  set,
  input  enable,
  input  clear,
  output clr,
  output [7:0] O
);

  wire cpu_dcode_2x4east_1_o0, cpu_dcode_2x4east_1_o1, cpu_dcode_2x4east_1_o2, cpu_dcode_2x4east_1_o3,
       cpu_dcode_2x4east_2_o0, cpu_dcode_2x4east_2_o1, cpu_dcode_2x4east_2_o2, cpu_dcode_2x4east_2_o3;
  wire [7:0] rem_reg_8_1_ireg, rem_reg_8_1_o, rem_reg_8_2_ireg, rem_reg_8_3_ireg, rem_reg_8_4_ireg,
       rem_reg_8_5_ireg, rem_reg_8_6_ireg, rem_reg_8_7_ireg, rem_reg_8_8_ireg, rem_reg_8_9_ireg,
       rem_reg_8_10_ireg, rem_reg_8_11_ireg, rem_reg_8_12_ireg, rem_reg_8_13_ireg, rem_reg_8_14_ireg,
       rem_reg_8_15_ireg, rem_reg_8_16_ireg;

  CPU_DCODE_2x4east cpu_dcode_2x4east_1 (
    .in_1(addr[1:0]), .O0(cpu_dcode_2x4east_1_o0), .O1(cpu_dcode_2x4east_1_o1), .O2(cpu_dcode_2x4east_1_o2),
    .O3(cpu_dcode_2x4east_1_o3));
  CPU_DCODE_2x4east cpu_dcode_2x4east_2 (
    .in_1(addr[3:2]), .O0(cpu_dcode_2x4east_2_o0), .O1(cpu_dcode_2x4east_2_o1), .O2(cpu_dcode_2x4east_2_o2),
    .O3(cpu_dcode_2x4east_2_o3));
  // Probe on rem_reg_8_1_ireg
  rem_reg_8 rem_reg_8_1 (
    .y(cpu_dcode_2x4east_2_o0), .x(cpu_dcode_2x4east_1_o0), .set(set), .ena(enable), .clr(clear), .i(I),
    .o(rem_reg_8_1_o), .ireg(rem_reg_8_1_ireg));
  // Probe on rem_reg_8_2_ireg
  rem_reg_8 rem_reg_8_2 (
    .y(cpu_dcode_2x4east_2_o1), .x(cpu_dcode_2x4east_1_o0), .set(set), .ena(enable), .clr(clear), .i(I),
    .o(rem_reg_8_1_o), .ireg(rem_reg_8_2_ireg));
  // Probe on rem_reg_8_3_ireg
  rem_reg_8 rem_reg_8_3 (
    .y(cpu_dcode_2x4east_2_o2), .x(cpu_dcode_2x4east_1_o0), .set(set), .ena(enable), .clr(clear), .i(I),
    .o(rem_reg_8_1_o), .ireg(rem_reg_8_3_ireg));
  // Probe on rem_reg_8_4_ireg
  rem_reg_8 rem_reg_8_4 (
    .y(cpu_dcode_2x4east_2_o3), .x(cpu_dcode_2x4east_1_o0), .set(set), .ena(enable), .clr(clear), .i(I),
    .o(rem_reg_8_1_o), .ireg(rem_reg_8_4_ireg));
  // Probe on rem_reg_8_5_ireg
  rem_reg_8 rem_reg_8_5 (
    .y(cpu_dcode_2x4east_2_o0), .x(cpu_dcode_2x4east_1_o1), .set(set), .ena(enable), .clr(clear), .i(I),
    .o(rem_reg_8_1_o), .ireg(rem_reg_8_5_ireg));
  // Probe on rem_reg_8_6_ireg
  rem_reg_8 rem_reg_8_6 (
    .y(cpu_dcode_2x4east_2_o1), .x(cpu_dcode_2x4east_1_o1), .set(set), .ena(enable), .clr(clear), .i(I),
    .o(rem_reg_8_1_o), .ireg(rem_reg_8_6_ireg));
  // Probe on rem_reg_8_7_ireg
  rem_reg_8 rem_reg_8_7 (
    .y(cpu_dcode_2x4east_2_o2), .x(cpu_dcode_2x4east_1_o1), .set(set), .ena(enable), .clr(clear), .i(I),
    .o(rem_reg_8_1_o), .ireg(rem_reg_8_7_ireg));
  // Probe on rem_reg_8_8_ireg
  rem_reg_8 rem_reg_8_8 (
    .y(cpu_dcode_2x4east_2_o3), .x(cpu_dcode_2x4east_1_o1), .set(set), .ena(enable), .clr(clear), .i(I),
    .o(rem_reg_8_1_o), .ireg(rem_reg_8_8_ireg));
  // Probe on rem_reg_8_9_ireg
  rem_reg_8 rem_reg_8_9 (
    .y(cpu_dcode_2x4east_2_o0), .x(cpu_dcode_2x4east_1_o2), .set(set), .ena(enable), .clr(clear), .i(I),
    .o(rem_reg_8_1_o), .ireg(rem_reg_8_9_ireg));
  // Probe on rem_reg_8_10_ireg
  rem_reg_8 rem_reg_8_10 (
    .y(cpu_dcode_2x4east_2_o1), .x(cpu_dcode_2x4east_1_o2), .set(set), .ena(enable), .clr(clear), .i(I),
    .o(rem_reg_8_1_o), .ireg(rem_reg_8_10_ireg));
  // Probe on rem_reg_8_11_ireg
  rem_reg_8 rem_reg_8_11 (
    .y(cpu_dcode_2x4east_2_o2), .x(cpu_dcode_2x4east_1_o2), .set(set), .ena(enable), .clr(clear), .i(I),
    .o(rem_reg_8_1_o), .ireg(rem_reg_8_11_ireg));
  // Probe on rem_reg_8_12_ireg
  rem_reg_8 rem_reg_8_12 (
    .y(cpu_dcode_2x4east_2_o3), .x(cpu_dcode_2x4east_1_o2), .set(set), .ena(enable), .clr(clear), .i(I),
    .o(rem_reg_8_1_o), .ireg(rem_reg_8_12_ireg));
  // Probe on rem_reg_8_13_ireg
  rem_reg_8 rem_reg_8_13 (
    .y(cpu_dcode_2x4east_2_o0), .x(cpu_dcode_2x4east_1_o3), .set(set), .ena(enable), .clr(clear), .i(I),
    .o(rem_reg_8_1_o), .ireg(rem_reg_8_13_ireg));
  // Probe on rem_reg_8_14_ireg
  rem_reg_8 rem_reg_8_14 (
    .y(cpu_dcode_2x4east_2_o1), .x(cpu_dcode_2x4east_1_o3), .set(set), .ena(enable), .clr(clear), .i(I),
    .o(rem_reg_8_1_o), .ireg(rem_reg_8_14_ireg));
  // Probe on rem_reg_8_15_ireg
  rem_reg_8 rem_reg_8_15 (
    .y(cpu_dcode_2x4east_2_o2), .x(cpu_dcode_2x4east_1_o3), .set(set), .ena(enable), .clr(clear), .i(I),
    .o(rem_reg_8_1_o), .ireg(rem_reg_8_15_ireg));
  // Probe on rem_reg_8_16_ireg
  rem_reg_8 rem_reg_8_16 (
    .y(cpu_dcode_2x4east_2_o3), .x(cpu_dcode_2x4east_1_o3), .set(set), .ena(enable), .clr(clear), .i(I),
    .o(rem_reg_8_1_o), .ireg(rem_reg_8_16_ireg));
  assign O = enable ? rem_reg_8_1_o : 8'bz;  // Controlled_Buffer controlled_buffer_1

  assign clr = clear;
endmodule

module CPU_DCODE_2x4east (
  input  [1:0] in_1,
  output O0,
  output O1,
  output O2,
  output O3
);

  wire not_1_out, not_2_out, not_3_out, not_4_out;

  not not_1 (not_1_out, in_1[0]);
  and and_1 (O0, not_1_out, not_2_out);
  not not_2 (not_2_out, in_1[1]);
  and and_2 (O1, in_1[0], not_3_out);
  not not_3 (not_3_out, in_1[1]);
  not not_4 (not_4_out, in_1[0]);
  and and_3 (O2, not_4_out, in_1[1]);
  and and_4 (O3, in_1[0], in_1[1]);
endmodule

module CPU_DCODE_2x4west (
  input  [1:0] in_1,
  output O0,
  output O1,
  output O2,
  output O3
);

  wire not_1_out, not_2_out, not_3_out, not_4_out;

  not not_1 (not_1_out, in_1[0]);
  and and_1 (O0, not_1_out, not_2_out);
  not not_2 (not_2_out, in_1[1]);
  and and_2 (O1, in_1[0], not_3_out);
  not not_3 (not_3_out, in_1[1]);
  not not_4 (not_4_out, in_1[0]);
  and and_3 (O2, not_4_out, in_1[1]);
  and and_4 (O3, in_1[0], in_1[1]);
endmodule

module ALU_8 (
  input  clr,
  input  [7:0] A,
  input  As,
  input  [7:0] B,
  input  Os,
  input  Oe,
  input  [3:0] sel,
  output [7:0] ro,
  output [7:0] ra,
  output [7:0] O,
  output C_out,
  output zero,
  output NEG
);

  wire and_1_out, and_2_out, and_3_out, and_4_out, and_5_out, and_6_out, comparator_8_1_a_greater,
       comparator_8_1_b_greater, comparator_8_1_equal, controlled_buffer_2_out, cpu_dcode_3x8_w_ena_1_o0,
       cpu_dcode_3x8_w_ena_1_o1, cpu_dcode_3x8_w_ena_1_o2, cpu_dcode_3x8_w_ena_1_o3, eightbitaddsub_1_c_out,
       eightbitaddsub_2_c_out, l_shift_1_c_out, l_shift_2_c_out, not_1_out, not_2_out, not_3_out, not_4_out,
       r_shift_1_c_out, r_shift_2_c_out, undriven_8, xor_1_out, xor_2_out;
  wire [1:0] undriven_7;
  wire [7:0] and_8_1_out_3, eightbitaddsub_1_result, eightbitaddsub_2_result, l_shift_2_o, mux_2x1_8bit_1_o,
       mux_4x1_8bit_1_o, mux_4x1_8bit_2_o, mux_8x1_8bit_1_o, mux_8x1_8bit_2_o, or_8_1_out_3, r_shift_1_o,
       r_shift_2_o, reg_8_1_o, undriven, undriven_2, undriven_3, undriven_4, undriven_5, undriven_6;

  reg_8 reg_8_1 (.i(A), .s(As), .e(1'b1), .clr(clr), .ireg(ra), .o(reg_8_1_o));
  Pull_Resistor pull_resistor_1 (.node(sel));
  Pull_Resistor pull_resistor_2 (.node(reg_8_1_o));
  Pull_Resistor pull_resistor_3 (.node(B));
  // Probe on ra
  Comparator_8 comparator_8_1 (
    .A(reg_8_1_o), .B(B), .B_Greater(comparator_8_1_b_greater), .A_Greater(comparator_8_1_a_greater),
    .Equal(comparator_8_1_equal));
  R_shift r_shift_1 (.I(reg_8_1_o), .O(r_shift_1_o), .C_out(r_shift_1_c_out));
  L_shift l_shift_1 (.I(reg_8_1_o), .C_out(l_shift_1_c_out));  // open: O
  R_shift r_shift_2 (.I(B), .O(r_shift_2_o), .C_out(r_shift_2_c_out));
  L_shift l_shift_2 (.I(B), .O(l_shift_2_o), .C_out(l_shift_2_c_out));
  AND_8 and_8_1 (.in_1(reg_8_1_o), .in_2(B), .out_3(and_8_1_out_3));
  OR_8 or_8_1 (.in_1(reg_8_1_o), .in_2(B), .out_3(or_8_1_out_3));
  EightBitAddSub eightbitaddsub_1 (
    .num1(reg_8_1_o), .num2(B), .subt(1'b0), .C_in(1'b0), .Result(eightbitaddsub_1_result),
    .C_out(eightbitaddsub_1_c_out));
  EightBitAddSub eightbitaddsub_2 (
    .num1(reg_8_1_o), .num2(B), .subt(1'b1), .C_in(1'b0), .Result(eightbitaddsub_2_result),
    .C_out(eightbitaddsub_2_c_out));
  and and_1 (and_1_out, cpu_dcode_3x8_w_ena_1_o0, sel[3]);
  assign C_out = and_1_out ? r_shift_1_c_out : 1'bz;  // Controlled_Buffer controlled_buffer_1
  assign controlled_buffer_2_out = and_4_out ? r_shift_2_c_out : 1'bz;  // Controlled_Buffer controlled_buffer_2
  assign C_out = and_3_out ? eightbitaddsub_1_c_out : 1'bz;  // Controlled_Buffer controlled_buffer_3
  assign C_out = and_2_out ? eightbitaddsub_2_c_out : 1'bz;  // Controlled_Buffer controlled_buffer_4
  not not_1 (not_1_out, sel[3]);
  and and_2 (and_2_out, not_1_out, cpu_dcode_3x8_w_ena_1_o3);
  not not_2 (not_2_out, sel[3]);
  and and_3 (and_3_out, not_2_out, cpu_dcode_3x8_w_ena_1_o2);
  and and_4 (and_4_out, cpu_dcode_3x8_w_ena_1_o2, sel[3]);
  and and_5 (and_5_out, sel[3], cpu_dcode_3x8_w_ena_1_o1);
  assign C_out = and_5_out ? l_shift_1_c_out : 1'bz;  // Controlled_Buffer controlled_buffer_5
  assign controlled_buffer_2_out = and_6_out ? l_shift_2_c_out : 1'bz;  // Controlled_Buffer controlled_buffer_6
  // Probe on and_8_1_out_3
  CPU_DCODE_3x8_w_ena cpu_dcode_3x8_w_ena_1 (
    .Sel(sel[2:0]), .enable(1'b1), .O0(cpu_dcode_3x8_w_ena_1_o0), .O1(cpu_dcode_3x8_w_ena_1_o1),
    .O2(cpu_dcode_3x8_w_ena_1_o2), .O3(cpu_dcode_3x8_w_ena_1_o3));  // open: O4, O5, O6, O7
  and and_6 (and_6_out, sel[3], cpu_dcode_3x8_w_ena_1_o3);
  Pull_Resistor pull_resistor_4 (.node(C_out));
  MUX_8x1_8bit mux_8x1_8bit_1 (
    .sel(sel[2:0]), .A(and_8_1_out_3), .B(or_8_1_out_3), .C(eightbitaddsub_1_result),
    .D(eightbitaddsub_2_result), .E(undriven_2), .F(undriven_3), .G(undriven_4), .H(undriven_5),
    .O(mux_8x1_8bit_1_o));
  MUX_8x1_8bit mux_8x1_8bit_2 (
    .sel(sel[2:0]), .A(r_shift_1_o), .B(undriven), .O(mux_8x1_8bit_2_o));  // open: C, D, E, F, G, H
  // Probe on {NEG, ro[6:0]}
  // Probe on mux_2x1_8bit_1_o
  MUX_2x1_8bit mux_2x1_8bit_1 (.sel(sel[3]), .A(mux_8x1_8bit_1_o), .B(mux_8x1_8bit_2_o), .O(mux_2x1_8bit_1_o));
  Comparator_8 comparator_8_2 (.A({NEG, ro[6:0]}), .B({8{1'b0}}), .Equal(zero));  // open: B_Greater, A_Greater
  reg_8 reg_8_2 (.i(mux_2x1_8bit_1_o), .s(Os), .e(Oe), .clr(clr), .ireg({NEG, ro[6:0]}), .o(O));
  ExactlyOne xor_1 (
    .out(xor_1_out), .in0(ro[0]), .in1(ro[1]), .in2(ro[2]), .in3(ro[3]), .in4(ro[4]), .in5(ro[5]),
    .in6(ro[6]), .in7(NEG));
  not not_3 (not_3_out, xor_1_out);
  // Probe on O
  ExactlyOne xor_2 (
    .out(xor_2_out), .in0(undriven_6[0]), .in1(undriven_6[1]), .in2(undriven_6[2]), .in3(undriven_6[3]),
    .in4(undriven_6[4]), .in5(undriven_6[5]), .in6(undriven_6[6]), .in7(undriven_6[7]));
  not not_4 (not_4_out, xor_2_out);
  // Probe on mux_4x1_8bit_1_o
  MUX_4x1_8bit mux_4x1_8bit_1 (.Sel(undriven_7), .O(mux_4x1_8bit_1_o));  // open: A, B, C, D
  MUX_4x1_8bit mux_4x1_8bit_2 (.Sel(undriven_7), .O(mux_4x1_8bit_2_o));  // open: A, B, C, D
  MUX_2x1_8bit mux_2x1_8bit_2 (.sel(undriven_8), .A(mux_4x1_8bit_1_o), .B(mux_4x1_8bit_2_o));  // open: O

  assign ro[7] = NEG;

  // Notes on the sheet:
  //   lw rd =mem[rs]
  //   sw mem[rs]= rd
  //   rd=rs
endmodule

module MAR (
  input  [7:0] i,
  input  s,
  input  clr,
  output [3:0] ireg,
  output [3:0] o
);

  wire [7:4] mem_8_1_o;

  mem_8 mem_8_1 (.e(s), .s(i), .clr(clr), .o({mem_8_1_o, ireg}));

  assign o = ireg;
endmodule
